// Logisim project HCountDiodes.circ as structural Verilog: 7 circuits, main circuit VDP
module VDP (
);

  wire and_1_out, and_2_out, and_3_out, and_4_out, and_5_out, button_2_out, clock_1_out, d_ff_1_q, d_ff_1_qn,
       d_ff_2_q, d_ff_3_q, n7451_1_pin6, n7451_1_pin8, n7451_2_pin6, n7451_2_pin8, n7451_2_pin10,
       n74153_1_pin1, n74153_3_pin1, n74153_3_pin3, n74153_3_pin4, n74153_3_pin7, n74153_3_pin9,
       n74153_3_pin15, n74157_2_pin4, n74157_2_pin7, n74157_2_pin9, n74157_2_pin12, n74157_3_pin15,
       n74157_4_pin15, n74161_1_pin1, n74161_1_pin3, n74161_1_pin11, n74161_1_pin12, n74161_1_pin13,
       n74161_2_pin1, n74161_2_pin7, n74161_2_pin15, n74161_3_pin1, n74161_3_pin10, n74161_3_pin14,
       n74166_1_pin1, n74166_1_pin2, n74166_1_pin3, n74166_1_pin4, n74166_1_pin5, n74166_1_pin6,
       n74166_1_pin9, n74166_1_pin10, n74166_1_pin11, n74166_1_pin12, n74166_1_pin13, n74166_1_pin14,
       n74166_1_pin15, n74175_1_pin4, n74175_1_pin5, n74175_1_pin12, n74175_1_pin13, n74273_1_pin11,
       n74273_2_pin1, nand_2_out, nand_3_out, nand_4_out, nand_5_out, nand_6_out, nand_7_out, nand_8_out,
       nand_9_out, nand_10_out, nand_11_out, nand_12_out, nand_13_out, nand_14_out, nand_15_out, nor_2_out,
       nor_3_out, nor_4_out, nor_5_out, nor_6_out, not_2_out, not_3_out, not_4_out, not_5_out, not_6_out,
       not_7_out, not_9_out, not_10_out, not_11_out, not_13_out, not_14_out, not_15_out, not_16_out,
       not_17_out, not_18_out, not_19_out, not_20_out, not_21_out, not_22_out, not_23_out, not_24_out,
       not_25_out, not_26_out, not_27_out, not_28_out, not_29_out, not_30_out, not_31_out, not_32_out,
       not_33_out, not_34_out, not_35_out, not_36_out, not_39_out, not_41_out, not_43_out, not_44_out,
       not_45_out, not_46_out, not_47_out, not_48_out, not_49_out, not_50_out, not_51_out, not_52_out,
       not_53_out, not_54_out, not_55_out, not_56_out, not_57_out, not_58_out, not_59_out, not_60_out,
       not_61_out, not_62_out, not_63_out, not_64_out, not_65_out, not_66_out, not_67_out, sn74ls170_1_q1,
       sn74ls170_1_q2, sn74ls170_1_q3, sn74ls170_1_q4, sn74ls393_2_qg, sn74ls393_2_qh;
  wire [2:0] not_8_out, sn74ls393_2_qa;
  wire [3:0] n74161_1_pin14, n74175_1_pin2;
  wire [5:0] n74157_2_pin2, sn74ls393_1_qa;
  wire [5:3] sn74ls393_2_qd;
  wire [7:0] multiplexer_2_out, multiplexer_3_out, n74157_2_pin3, n74273_1_pin2, n74273_1_pin3,
       rgb_video_1_p6, rom_1_data, rom_2_data;
  wire [7:2] n74161_2_pin5;
  wire [8:0] rgb_video_1_p4, rgb_video_1_p5;
  wire [15:0] n74157_1_pin4;

  // NAND_Gate nand_1 is placed but not wired
  // NOR_Gate nor_1 is placed but not wired
  Clock clock_1 (.out(clock_1_out));
  // NOT_Gate not_1 is placed but not wired
  _74161 #(.ShowInternalStructure("true")) u_74161_1 (
    .pin1(n74161_1_pin1), .pin2(clock_1_out), .pin3(n74161_1_pin3), .pin4(n74161_1_pin3),
    .pin5(n74161_1_pin3), .pin6(n74161_1_pin3), .pin7(n74161_1_pin3), .pin14(n74161_1_pin14[0]),
    .pin13(n74161_1_pin13), .pin12(n74161_1_pin12), .pin11(n74161_1_pin11), .pin10(n74161_1_pin3),
    .pin9(n74161_1_pin3));  // open: pin15
  SN74LS393 sn74ls393_1 (
    .nCLK1(not_33_out), .CLR1(not_6_out), .nCLK2(sn74ls393_1_qa[3]), .CLR2(not_6_out),
    .QA(sn74ls393_1_qa[0]), .QB(sn74ls393_1_qa[1]), .QC(sn74ls393_1_qa[2]), .QD(sn74ls393_1_qa[3]),
    .QE(sn74ls393_1_qa[4]), .QF(sn74ls393_1_qa[5]));  // open: QG, QH
  SN74LS393 sn74ls393_2 (
    .nCLK1(nand_8_out), .CLR1(not_26_out), .nCLK2(sn74ls393_2_qd[3]), .CLR2(not_26_out),
    .QA(sn74ls393_2_qa[0]), .QB(sn74ls393_2_qa[1]), .QC(sn74ls393_2_qa[2]), .QD(sn74ls393_2_qd[3]),
    .QE(sn74ls393_2_qd[4]), .QF(sn74ls393_2_qd[5]), .QG(sn74ls393_2_qg), .QH(sn74ls393_2_qh));
  not not_2 (not_2_out, sn74ls393_2_qh);
  D_Flip_Flop d_ff_1 (.clk(not_2_out), .D(1'b1), .Q(d_ff_1_q), .Qn(d_ff_1_qn), .reset(not_3_out));  // open: preset
  not not_3 (not_3_out, nand_9_out);
  and and_1 (and_1_out, n74161_1_pin11, n74161_1_pin12, n74161_1_pin13, n74161_1_pin14[0]);
  nand nand_2 (nand_2_out, sn74ls393_1_qa[5], sn74ls393_1_qa[4]);
  not not_4 (not_4_out, nand_2_out);
  not not_5 (not_5_out, not_4_out);
  nand nand_3 (nand_3_out, sn74ls393_1_qa[0], sn74ls393_1_qa[3], sn74ls393_1_qa[4], sn74ls393_1_qa[5]);
  not not_6 (not_6_out, nand_3_out);
  nand nand_4 (nand_4_out, sn74ls393_2_qh, sn74ls393_2_qg);
  not not_7 (not_7_out, sn74ls393_2_qd[5]);
  not not_8 (not_8_out[0], nand_5_out);
  nand nand_5 (nand_5_out, n74161_2_pin5[3], n74161_2_pin5[2]);
  not not_9 (not_9_out, n74161_2_pin5[3]);
  nand nand_6 (nand_6_out, not_9_out, n74161_2_pin5[2]);
  nor nor_2 (nor_2_out, sn74ls393_1_qa[4], sn74ls393_1_qa[2]);
  nand nand_7 (nand_7_out, not_4_out, not_11_out);
  not not_10 (not_10_out, not_5_out);
  not not_11 (not_11_out, not_10_out);
  and and_2 (and_2_out, sn74ls393_2_qa[2], sn74ls393_2_qd[3], sn74ls393_2_qd[4], not_7_out, nand_4_out);
  not not_12 (n74161_1_pin14[3], and_2_out);
  and and_3 (and_3_out, sn74ls393_1_qa[0], sn74ls393_1_qa[1], sn74ls393_1_qa[3], sn74ls393_1_qa[5]);
  not not_13 (not_13_out, not_14_out);
  not not_14 (not_14_out, not_15_out);
  not not_15 (not_15_out, not_17_out);
  not not_16 (not_16_out, n74157_1_pin4[7]);
  nand nand_8 (nand_8_out, and_3_out, nor_2_out);
  nand nand_9 (nand_9_out, sn74ls393_2_qa[1], sn74ls393_2_qa[2], d_ff_1_q, d_ff_1_q);
  _74161 #(.ShowInternalStructure("true")) u_74161_2 (
    .pin1(n74161_2_pin1), .pin2(not_13_out), .pin3(not_8_out[0]), .pin4(not_8_out[1]),
    .pin5(n74161_2_pin5[2]), .pin6(nand_6_out), .pin7(n74161_2_pin7), .pin15(n74161_2_pin15),
    .pin14(n74157_1_pin4[8]), .pin13(n74157_1_pin4[9]), .pin12(n74157_1_pin4[10]), .pin11(n74157_1_pin4[11]),
    .pin10(n74161_2_pin7), .pin9(d_ff_1_qn));
  _74161 #(.ShowInternalStructure("true")) u_74161_3 (
    .pin1(n74161_3_pin1), .pin2(not_13_out), .pin3(n74161_2_pin5[4]), .pin4(n74161_2_pin5[5]),
    .pin5(n74161_2_pin5[6]), .pin6(n74161_2_pin5[7]), .pin7(n74161_2_pin15), .pin14(n74161_3_pin14),
    .pin13(n74157_1_pin4[13]), .pin12(n74157_1_pin4[14]), .pin11(n74157_1_pin4[15]), .pin10(n74161_3_pin10),
    .pin9(d_ff_1_qn));  // open: pin15
  not not_17 (not_17_out, not_18_out);
  not not_18 (not_18_out, not_19_out);
  not not_19 (not_19_out, not_20_out);
  not not_20 (not_20_out, not_27_out);
  not not_21 (not_21_out, not_16_out);
  not not_22 (not_22_out, not_21_out);
  not not_23 (not_23_out, not_22_out);
  not not_24 (not_24_out, not_23_out);
  _74273 #(.ShowInternalStructure("true")) u_74273_1 (
    .pin2(n74273_1_pin2[0]), .pin3(n74273_1_pin3[0]), .pin4(n74273_1_pin3[1]), .pin5(n74273_1_pin2[1]),
    .pin6(n74273_1_pin2[2]), .pin7(n74273_1_pin3[2]), .pin8(n74273_1_pin3[3]), .pin9(n74273_1_pin2[3]),
    .pin19(n74273_1_pin2[7]), .pin18(n74273_1_pin3[7]), .pin17(n74273_1_pin3[6]), .pin16(n74273_1_pin2[6]),
    .pin15(n74273_1_pin2[5]), .pin14(n74273_1_pin3[5]), .pin13(n74273_1_pin3[4]), .pin12(n74273_1_pin2[4]),
    .pin11(n74273_1_pin11));  // open: pin1
  not not_25 (not_25_out, d_ff_1_q);
  not not_26 (not_26_out, nand_9_out);
  not not_27 (not_27_out, not_28_out);
  not not_28 (not_28_out, not_31_out);
  not not_29 (not_29_out, not_24_out);
  not not_30 (not_30_out, not_29_out);
  not not_31 (not_31_out, not_30_out);
  Button button_1 (.out(n74273_1_pin11));
  Timer_555 timer_555_1 (.Count(8'hce), .Trigger(nand_8_out), .DOut(n74161_1_pin14[1]));
  not not_32 (not_32_out, sn74ls393_1_qa[0]);
  nand nand_10 (nand_10_out, nand_4_out, not_25_out);
  Timer_555 timer_555_2 (.Count(8'he0), .Trigger(nand_7_out), .DOut(n74161_1_pin14[2]));
  nor nor_3 (nor_3_out, not_32_out, n74161_1_pin11);
  nor nor_4 (nor_4_out, sn74ls393_1_qa[5], nand_10_out);
  not not_33 (not_33_out, n74161_1_pin11);
  D_Flip_Flop d_ff_2 (.clk(nor_3_out), .D(nor_4_out), .Q(d_ff_2_q));  // open: Qn, preset, reset
  not not_34 (not_34_out, not_8_out[1]);
  not not_35 (not_35_out, n74153_1_pin1);
  _74153 #(.ShowInternalStructure("true")) u_74153_1 (
    .pin1(n74153_1_pin1), .pin2(n74161_2_pin5[3]), .pin15(n74153_1_pin1), .pin14(n74161_2_pin5[2]),
    .pin13(sn74ls393_2_qd[5]), .pin12(sn74ls393_2_qd[4]), .pin11(sn74ls393_2_qd[3]),
    .pin10(sn74ls393_2_qa[2]), .pin9(n74157_1_pin4[7]));  // open: pin3, pin4, pin5, pin6, pin7
  not not_36 (not_36_out, d_ff_2_q);
  _74157 #(.ShowInternalStructure("true")) u_74157_1 (
    .pin1(not_8_out[1]), .pin2(sn74ls393_1_qa[0]), .pin3(sn74ls393_1_qa[1]), .pin4(n74157_1_pin4[0]),
    .pin5(sn74ls393_1_qa[1]), .pin6(sn74ls393_1_qa[2]), .pin7(n74157_1_pin4[1]), .pin15(n74153_1_pin1),
    .pin14(sn74ls393_1_qa[3]), .pin13(sn74ls393_1_qa[4]), .pin12(n74157_1_pin4[3]),
    .pin11(sn74ls393_1_qa[2]), .pin10(sn74ls393_1_qa[3]), .pin9(n74157_1_pin4[2]));
  _7451 #(.ShowInternalStructure("true")) u_7451_1 (
    .pin1(not_34_out), .pin2(n74153_1_pin1), .pin3(sn74ls393_2_qd[3]), .pin4(not_35_out),
    .pin5(n74161_3_pin14), .pin6(n7451_1_pin6), .pin13(sn74ls393_1_qa[4]), .pin10(not_8_out[1]),
    .pin9(sn74ls393_2_qa[1]), .pin8(n7451_1_pin8));  // open: pin12, pin11
  nand nand_11 (nand_11_out, not_36_out, not_8_out[0]);
  not not_37 (n74157_1_pin4[4], n7451_1_pin8);
  _74153 #(.ShowInternalStructure("true")) u_74153_2 (
    .pin1(n74153_1_pin1), .pin2(n74161_2_pin5[3]), .pin3(sn74ls393_2_qd[4]), .pin4(sn74ls393_2_qd[3]),
    .pin5(sn74ls393_2_qa[2]), .pin6(sn74ls393_2_qa[1]), .pin7(n74157_1_pin4[6]), .pin15(n74153_1_pin1),
    .pin14(n74161_2_pin5[2]), .pin13(sn74ls393_2_qd[3]), .pin12(sn74ls393_2_qa[2]),
    .pin11(sn74ls393_2_qa[1]), .pin10(sn74ls393_2_qa[0]), .pin9(n74157_1_pin4[5]));
  not not_38 (n74157_1_pin4[12], n7451_1_pin6);
  not not_39 (not_39_out, not_8_out[2]);
  _7451 #(.ShowInternalStructure("true")) u_7451_2 (
    .pin1(n74161_1_pin13), .pin2(n74161_1_pin13), .pin3(not_8_out[2]), .pin4(n74161_1_pin14[0]),
    .pin5(not_39_out), .pin6(n7451_2_pin6), .pin13(not_8_out[1]), .pin10(n7451_2_pin10),
    .pin9(n74161_1_pin14[0]), .pin8(n7451_2_pin8));  // open: pin12, pin11
  _74175 #(.ShowInternalStructure("true")) u_74175_1 (
    .pin1(d_ff_2_q), .pin2(n74175_1_pin2[0]), .pin4(n74175_1_pin4), .pin5(n74175_1_pin5),
    .pin7(n74175_1_pin2[1]), .pin15(n74175_1_pin2[3]), .pin13(n74175_1_pin13), .pin12(n74175_1_pin12),
    .pin10(n74175_1_pin2[2]), .pin9(n7451_2_pin6));  // open: pin3, pin6, pin14, pin11
  not not_40 (n7451_2_pin10, not_8_out[1]);
  xor xor_1 (n74175_1_pin13, n74166_1_pin13, sn74ls170_1_q4);
  xor xor_2 (n74175_1_pin12, n74166_1_pin13, sn74ls170_1_q3);
  xor xor_3 (n74175_1_pin5, n74166_1_pin13, sn74ls170_1_q2);
  xor xor_4 (n74175_1_pin4, n74166_1_pin13, sn74ls170_1_q1);
  D_Flip_Flop d_ff_3 (.clk(n7451_2_pin8), .D(n74166_1_pin13), .Q(d_ff_3_q), .reset(not_41_out));  // open: Qn, preset
  not not_41 (not_41_out, not_8_out[2]);
  SN74LS170 sn74ls170_1 (
    .D1(n74157_2_pin4), .D2(n74157_2_pin7), .D3(n74157_2_pin9), .D4(n74157_2_pin12), .RB(n74166_1_pin13),
    .RA(d_ff_3_q), .nGR(1'b0), .nGW(not_57_out), .WB(n74153_3_pin9), .WA(n74153_3_pin7), .Q1(sn74ls170_1_q1),
    .Q2(sn74ls170_1_q2), .Q3(sn74ls170_1_q3), .Q4(sn74ls170_1_q4));
  _74166 #(.ShowInternalStructure("true")) u_74166_1 (
    .pin1(n74166_1_pin1), .pin2(n74166_1_pin2), .pin3(n74166_1_pin3), .pin4(n74166_1_pin4),
    .pin5(n74166_1_pin5), .pin6(n74166_1_pin6), .pin7(n7451_2_pin8), .pin15(n74166_1_pin15),
    .pin14(n74166_1_pin14), .pin13(n74166_1_pin13), .pin12(n74166_1_pin12), .pin11(n74166_1_pin11),
    .pin10(n74166_1_pin10), .pin9(n74166_1_pin9));
  nand nand_12 (nand_12_out, sn74ls393_1_qa[0], not_8_out[1]);
  not not_42 (n74166_1_pin15, nor_5_out);
  not not_43 (not_43_out, nand_11_out);
  nor nor_5 (nor_5_out, not_53_out, nand_13_out);
  not not_44 (not_44_out, not_56_out);
  not not_45 (not_45_out, not_43_out);
  not not_46 (not_46_out, not_45_out);
  not not_47 (not_47_out, not_46_out);
  not not_48 (not_48_out, not_47_out);
  not not_49 (not_49_out, and_1_out);
  not not_50 (not_50_out, not_49_out);
  not not_51 (not_51_out, not_50_out);
  not not_52 (not_52_out, not_51_out);
  not not_53 (not_53_out, not_52_out);
  _74157 #(.ShowInternalStructure("true")) u_74157_2 (
    .pin1(not_8_out[0]), .pin2(n74157_2_pin2[0]), .pin3(n74157_2_pin3[0]), .pin4(n74157_2_pin4),
    .pin5(n74157_2_pin2[1]), .pin6(n74157_2_pin3[1]), .pin7(n74157_2_pin7), .pin15(not_44_out),
    .pin14(n74157_2_pin2[3]), .pin13(n74157_2_pin3[3]), .pin12(n74157_2_pin12), .pin11(n74157_2_pin2[2]),
    .pin10(n74157_2_pin3[2]), .pin9(n74157_2_pin9));
  not not_54 (not_54_out, not_48_out);
  not not_55 (not_55_out, not_54_out);
  not not_56 (not_56_out, not_55_out);
  nand nand_13 (nand_13_out, nand_12_out, nand_15_out);
  _74153 #(.ShowInternalStructure("true")) u_74153_3 (
    .pin1(n74153_3_pin1), .pin2(not_8_out[0]), .pin3(n74153_3_pin3), .pin4(n74153_3_pin4),
    .pin5(n74157_2_pin2[5]), .pin6(n74157_2_pin2[5]), .pin7(n74153_3_pin7), .pin15(n74153_3_pin15),
    .pin14(nand_11_out), .pin13(n74157_2_pin3[4]), .pin12(n74161_1_pin11), .pin11(n74157_2_pin2[4]),
    .pin10(n74157_2_pin2[4]), .pin9(n74153_3_pin9));
  // Random random_1: pin names not known; wires that end beside it: 1'b1, n74161_1_pin11
  not not_57 (not_57_out, nand_14_out);
  nand nand_14 (nand_14_out, button_2_out, nand_11_out, nand_15_out);
  nand nand_15 (nand_15_out, not_33_out, not_8_out[0], nor_6_out, n74157_2_pin3[7]);
  nor nor_6 (nor_6_out, n74157_2_pin3[5], n74157_2_pin3[6]);
  ROM #(.addrWidth(11)) rom_1 (.addr({n74157_2_pin3, sn74ls393_2_qa}), .data(rom_1_data));
  _74157 #(.ShowInternalStructure("true")) u_74157_3 (
    .pin1(not_8_out[0]), .pin2(n74157_2_pin3[4]), .pin3(rom_1_data[4]), .pin4(n74166_1_pin10),
    .pin5(n74157_2_pin3[5]), .pin6(rom_1_data[5]), .pin7(n74166_1_pin11), .pin15(n74157_3_pin15),
    .pin14(n74157_2_pin3[7]), .pin13(rom_1_data[7]), .pin12(n74166_1_pin14), .pin11(n74157_2_pin3[6]),
    .pin10(rom_1_data[6]), .pin9(n74166_1_pin12));
  _74157 #(.ShowInternalStructure("true")) u_74157_4 (
    .pin1(not_8_out[0]), .pin2(n74157_2_pin3[0]), .pin3(rom_1_data[0]), .pin4(n74166_1_pin2),
    .pin5(n74157_2_pin3[1]), .pin6(rom_1_data[1]), .pin7(n74166_1_pin3), .pin15(n74157_4_pin15),
    .pin14(n74157_2_pin3[3]), .pin13(rom_1_data[3]), .pin12(n74166_1_pin5), .pin11(n74157_2_pin3[2]),
    .pin10(rom_1_data[2]), .pin9(n74166_1_pin4));
  // Probe on n74157_1_pin4[10:0]
  // Probe on n74157_1_pin4
  ROM #(.addrWidth(11)) rom_2 (.addr(n74157_1_pin4[10:0]), .data(rom_2_data));
  _74273 #(.ShowInternalStructure("true")) u_74273_2 (
    .pin1(n74273_2_pin1), .pin2(n74157_2_pin3[0]), .pin3(rom_2_data[0]), .pin4(rom_2_data[1]),
    .pin5(n74157_2_pin3[1]), .pin6(n74157_2_pin3[2]), .pin7(rom_2_data[2]), .pin8(rom_2_data[3]),
    .pin9(n74157_2_pin3[3]), .pin19(n74157_2_pin3[7]), .pin18(rom_2_data[7]), .pin17(rom_2_data[6]),
    .pin16(n74157_2_pin3[6]), .pin15(n74157_2_pin3[5]), .pin14(rom_2_data[5]), .pin13(rom_2_data[4]),
    .pin12(n74157_2_pin3[4]), .pin11(n74161_1_pin11));
  Button #(.press("passive")) button_2 (.out(button_2_out));
  // RGB_Video #(.cursor("No Cursor"), .height(262), .scale(1), .width(458)) rgb_video_1: pin names not known; wires that end beside it: 1'b0, n74161_1_pin14[0], 1'b1, rgb_video_1_p4, rgb_video_1_p5, rgb_video_1_p6
  Multiplexer #(.width(8)) multiplexer_1 (
    .in0(multiplexer_2_out), .in1(8'hc), .out(rgb_video_1_p6), .sel(n74161_1_pin14[3]));
  Multiplexer #(.width(8)) multiplexer_2 (
    .in0(multiplexer_3_out), .in1(8'hd), .out(multiplexer_2_out), .sel(n74161_1_pin14[1]));
  Multiplexer #(.width(8)) multiplexer_3 (
    .in0({4'b0000, n74175_1_pin2}), .in1(8'hb), .out(multiplexer_3_out), .sel(n74161_1_pin14[2]));
  Counter #(.max('h1ff), .width(9)) counter_1 (
    .load(1'b0), .count(1'b1), .Q(rgb_video_1_p5), .up(1'b1), .clk(n74161_1_pin14[1]), .clr(and_4_out));  // open: D, carry
  and and_4 (and_4_out, n74161_1_pin14[3], not_58_out);
  not not_58 (not_58_out, not_59_out);
  not not_59 (not_59_out, not_60_out);
  not not_60 (not_60_out, not_61_out);
  not not_61 (not_61_out, not_62_out);
  not not_62 (not_62_out, n74161_1_pin14[3]);
  Counter #(.max('h1ff), .width(9)) counter_2 (
    .load(1'b0), .count(1'b1), .Q(rgb_video_1_p4), .up(1'b1), .clk(n74161_1_pin14[0]), .clr(and_5_out));  // open: D, carry
  and and_5 (and_5_out, n74161_1_pin14[1], not_63_out);
  not not_63 (not_63_out, not_64_out);
  not not_64 (not_64_out, not_65_out);
  not not_65 (not_65_out, not_66_out);
  not not_66 (not_66_out, not_67_out);
  not not_67 (not_67_out, n74161_1_pin14[1]);
  // also tied to GND on the sheet: {n74273_1_pin3[0], n74273_1_pin3[1], n74273_1_pin3[2], n74273_1_pin3[3], n74273_1_pin3[4], n74273_1_pin3[5], n74273_1_pin3[6], n74273_1_pin3[7], not_8_out[2:1], n74161_2_pin5[4], n74161_2_pin5[5], n74161_2_pin5[6], n74161_2_pin5[7], n74153_1_pin1, n74166_1_pin1, n74166_1_pin6, n74153_3_pin4, n74153_3_pin3, n74153_3_pin15, n74153_3_pin1, n74157_3_pin15, n74157_4_pin15}
  // also tied to VCC on the sheet: {n74161_1_pin1, n74161_1_pin3, n74161_2_pin5[2], n74161_2_pin5[3], n74161_2_pin1, n74161_2_pin7, n74161_3_pin1, n74161_3_pin10, n74166_1_pin9, n74273_2_pin1}

  // Notes on the sheet:
  //   CLK
  //   14.31818 MHz
  //   U36C
  //   U36D
  //   U44D
  //   U38B
  //   U38C
  //   U38D
  //   /CLK
  //   U47F
  //   In Shielded Can
  //   \edge
  //   U30
  //   nHsync
  //   U33E
  //   and
  //   and
  //   U62
  //   (74LS393 is \edge triggered)
  //   6-bit H-Count
  //   U34
  //   U37B
  //   active low
  //   Text
  //   HSel
  //   2Bpp
  //   ModeReg
  //   ModeReg
  //   MUST update Address on /CLK mid-cycle
  //   1 load
  //   U32A
  //   (included)
  //   192
  //   U32C
  //   U33F
  //   U39E
  //   U44B
  //   7.15909 MHz
  //   3.579545 MHz
  //   1.7897725 MHz
  //   0.894886 MHz
  //   [0-56]
  //   U35A
  //   U33B
  //   U31A
  //   3 loads
  //   diode-AND 4.7k
  //   0111xx
  //   TextMode
  //   U39D
  //   U44A
  //   Work-around for incorrectly timed RCO output
  //   Not in BOM
  //   1 in 16
  //   101011
  //   11xxxx
  //   111001
  //   3 loads
  //   diode-AND 4.7k
  //   RC+pullup pulse
  //   Rst (57)
  //   111001
  //   U39A
  //   HSel
  //   Schmitt
  //   1 load (in common)
  //   falling edge
  //   \PageCross
  //   triple NAND low + RC pullup
  //   quad NAND low + Inverter
  //   101011
  //   U32B
  //   nBurst (48)
  //   110000
  //   Vsync (220)
  //   nRst
  //   U31B
  //   VC 0-3
  //   U42
  //   VC 4-5
  //   U43
  //   RC Delay
  //   Allow time for nRst decode
  //   U63
  //   ModeReg
  //   quad NAND + triple NOR high + Inverter
  //   Diode Logic to decode 1s (pull-down diodes + pullup to 5V + clamp diode + inverter)
  //   Diode Logic to decode 1s (pull-up diodes + pulldown to GND + clamp diode + inverter)
  //   nHsync (43)
  //   1xxxx
  //   256
  //   or
  //   U39B
  //   U32D
  //   U39C
  //   IOW_ VDP
  //   1 load
  //   U40
  //   U33C
  //   and
  //   U35B
  //   Border (32)
  //   3 loads + 2 loads (ROM)
  //   nVvis
  //   Vsync
  //   Rst (262)
  //   nRst
  //   /LD while CLK=0 is bad
  //   (safe: \LD while CLK=0 -> CLK=1)
  //   (safe: CLK stays high until V5=1, 63 lines)
  //   192 and 0111xx
  //   256 and xxx11x
  //   HSync (4.7μs, 4.18 CLK)
  //   U41
  //   /T=1.5
  //   V1
  //   U33A
  //   triple NAND low
  //   Burst (2.8µs, 2.49 CLK)
  //   and
  //   U35C
  //   V3
  //   Refresh
  //   Vsel0
  //   Vsel1
  //   triple NAND + Inverter + triple NOR high
  //   Visible
  //   U37A
  //   HSel
  //   U39F
  //   U47A
  //   V5432
  //   U45
  //   U33D
  //   H4
  //   nRefresh
  //   1 load
  //   HCount
  //   2 loads
  //   U36A
  //   V1
  //   VC4
  //   U61
  //   U47B
  //   U62
  //   V4321
  //   V3210
  //   U46
  //   VDP Address
  //   U47C
  //   PCLK
  //   HSync
  //   Burst
  //   VSync
  //   nClrCol
  //   TextMode
  //   Text
  //   Wide
  //   2Bpp
  //   Mode
  //   RCO (15)
  //   7.15909 MHz
  //   3.579545 MHz
  //   U66E
  //   2BPP
  //   Video Out
  //   VDP Address
  //   Vcount
  //   U58
  //   Pixel Color
  //   HSel
  //   In Shielded Can
  //   U59
  //   In Shielded Can
  //   LATCH on /PWCLK edge
  //   DAC Latch
  //   Force to 0 outside
  //   display area
  //   U66F
  //   00 -> 00
  //   01 -> 01
  //   10 -> 10
  //   11 -> 11
  //   In Shielded Can
  //   \PWCLK
  //   2BPP
  //   In Shielded Can
  //   Invert FG 0000 -> 1111
  //   U51
  //   U57
  //   2BPP D1
  //   U60A
  //   Active Low
  //   Requires Pullups
  //   Check Palette latch timing vs VDP Latch
  //   SHIFT on \PCLK edge
  //   LOAD on \CLK at last \PCLK edge
  //   Shift Register
  //   nLoad
  //   In Shielded Can
  //   Palette Registers
  //   In Shielded Can
  //   U48
  //   In Shielded Can
  //   and
  //   U44C
  //   8x 00 -> 00
  //   9x 01 -> 10
  //   /TC\ spans high half of last PCLK before \CLK
  //   U47E
  //   Schmitt
  //   nWideOdd (inhibit)
  //   U35D
  //   High Strobe lock outputs low
  //   U49
  //   RC Delay
  //   Sustain locked outputs across /nClrCol edge
  //   to pervent latching from VDP Latch
  //   Schmitt
  //   U36B
  //   U50
  //   TextMode
  //   Random Data Bus
  //   RC Delay: make /TC\ span across \PCLK edge
  //   nAttrLd (inhibit)
  //   TextMode
  //   nClrCol
  //   nClrCol
  //   CLK
  //   8x/9x
  //   nLoadPal
  //   Normally High
  //   U47D
  //   LoadQ on \CLK
  //   00 -> 01 (1)
  //   01 -> 00 (0)
  //   10 -> 11 (3)
  //   11 -> 10 (2)
  //   nWRpal
  //   or
  //   U52B
  //   LoadQ on \CLK
  //   Held until /CLK
  //   nAttrLd
  //   and
  //   U52A
  //   8x/9x (100x)
  //   Low 4 bits
  //   Bus CLK 0.89 MHz
  //   and
  //   U38A
  //   TextMode
  //   V[0..2]
  //   U56
  //   contents of rom_1 (hex, n*v repeats v):
  //   aa 55 aa 55 aa 55 aa 55 aa 41 aa 4 aa 10 aa 4 aa 0 aa 0 aa 0 aa 0 88 0 a2 0 24 0 8a 0 8 0 82 0 0 20
  //   2 4*0 1f 1f 18 18 18 0 0 0 f8 f8 6*18 1f 1f 0 0 0 18 18 18 f8 f8 6*0 ff ff 0 0 0 11*18 ff ff 6*0 ff
  //   ff 6*18 1f 1f 6*18 f8 f8 6*18 ff ff 18 18 18 1 3 6 c 18 30 60 c0 80 c0 60 30 18 c 6 3 c0 60 30 18 c
  //   6 3 1 3 6 c 18 30 60 c0 80 c3 66 2c 18 34 66 c3 81 0 0 18 3c 3c 18 4*0 18 24 24 18 0 0 10 38 7c fe
  //   7c 38 10 0 10 38 54 fe 54 10 38 0 44 ee fe fe 7c 38 10 0 10 38 7c fe 6c 10 38 0 0 2 0 0 10 1 5*0 8
  //   7*0 18 18 0 0 0 cc 66 33 99 cc 66 33 99 33 66 cc 99 33 66 cc 99 9*0 18 18 18 0 18 18 0 0 36 36 5*0
  //   36 36 7f 36 7f 36 36 0 8 3e 68 3e b 3e 8 0 21 52 24 8 12 25 42 0 30 48 68 30 5b 4c 36 0 18 18 30 5*0
  //   18 30 60 60 60 30 18 0 c 6 3 3 3 6 c 0 0 36 1c 7f 1c 36 0 0 0 c c 3f c c 6*0 18 18 30 5*0 3f 8*0 18
  //   18 0 0 3 6 c 18 30 60 0 0 3c 66 6e 76 66 3c 0 0 18 38 78 18 18 7e 0 0 3c 66 c 18 30 7e 0 0 3c 66 c 6
  //   66 3c 0 0 c 1c 2c 6c 7e c 0 0 7e 60 7c 6 66 3c 0 0 3c 60 7c 66 66 3c 0 0 7e 6 c 18 30 30 0 0 3c 66
  //   3c 66 66 3c 0 0 3c 66 66 3e 6 3c 0 0 0 c c 0 c c 0 0 0 c c 0 c 18 0 0 6 c 18 18 c 6 0 0 0 3e 0 3e
  //   4*0 30 18 c c 18 30 0 0 3c 66 c 18 0 18 0 1e 21 4d 55 4a 20 1e 0 0 3c 66 7e 66 66 66 0 0 7c 66 7c 66
  //   66 7c 0 0 3c 66 60 60 66 3c 0 0 78 6c 66 66 6c 78 0 0 7e 60 7c 60 60 7e 0 0 7e 60 7c 60 60 60 0 0 3c
  //   66 60 6e 66 3c 0 0 66 66 7e 66 66 66 0 0 7e 4*18 7e 0 0 3e c c c 6c 38 0 0 66 6c 78 78 6c 66 0 0
  //   5*60 7e 0 0 63 77 7f 6b 63 63 0 0 66 76 7e 6e 66 66 0 0 3c 4*66 3c 0 0 7c 66 66 7c 60 60 0 0 3c 66
  //   66 6a 6c 36 0 0 7c 66 66 7c 6c 66 0 0 3c 62 3c 6 66 3c 0 0 7e 5*18 0 0 5*66 3c 0 0 4*66 3c 18 0 0 63
  //   63 6b 7f 77 63 0 0 66 66 3c 3c 66 66 0 0 66 66 3c 18 18 18 0 0 7e c 18 30 60 7e 0 0 7c 4*60 7c 0 0
  //   60 30 18 c 6 3 0 0 3e 4*6 3e 0 0 18 3c 66 11*0 7f 0 60 30 18 6*0 3c 6 3e 66 3c 0 0 60 7c 66 66 66 7c
  //   0 0 0 3c 66 60 66 3c 0 0 6 3e 66 66 66 3e 0 0 0 3c 66 7c 60 3c 0 0 1e 30 7c 30 30 30 0 0 0 3c 66 66
  //   3e 6 3c 0 60 60 6c 76 66 66 0 0 18 0 38 18 18 3c 0 0 c 0 1c c c 6c 38 0 60 66 6c 78 6c 66 0 0 38
  //   4*18 3c 0 0 0 36 7f 6b 6b 63 0 0 0 7c 4*66 0 0 0 3c 66 66 66 3c 0 0 0 7c 66 66 7c 60 60 0 0 3e 66 66
  //   3e 6 6 0 0 6c 76 60 60 60 0 0 0 3c 60 3c 6 3c 0 0 30 7c 30 30 30 1c 0 0 0 4*66 3c 0 0 0 66 66 66 3c
  //   18 0 0 0 63 6b 6b 7f 36 0 0 0 66 3c 18 3c 66 0 0 0 66 66 66 3e 6 3c 0 0 7e c 18 30 7e 0 0 6 c c 18 c
  //   c 6 0 7*18 0 30 18 18 c 18 18 30 0 0 0 31 6b 46 5*0 18 24 42 42 7e 256*0 1 3 7 f 1f 3f 7f ff 80 c0
  //   e0 f0 f8 fc fe ff 4*0 1 3 7 f 4*0 80 c0 e0 f0 1 2 4 8 10 20 40 80 80 40 20 10 8 4 2 1 4*0 1 2 4 8
  //   4*0 80 40 20 10 0 3c 42 81 24 e7 3c 1 ff 7*80 ff 7*0 ff 7*1 ff 6*81 ff 18 24 42 81 81 42 24 18 18 18
  //   3c 3c 7e 7e ff ff 18 18 24 24 42 42 81 81 ff 7f 3f 1f f 7 3 1 ff fe fc f8 f0 e0 c0 80 f 7 3 1 4*0 f0
  //   e0 c0 80 4*0 80 40 20 10 8 4 2 1 1 2 4 8 10 20 40 80 8 4 2 1 4*0 10 20 40 80 4*0 e3 95 89 a2 bc a0
  //   a0 0 8*80 a5 0 81 0 0 81 0 a5 8*1 0 0 3c 24 24 3c 0 0 18 3c 7e ff ff 7e 3c 18 ff ff 7e 7e 3c 3c 18
  //   18 81 81 42 42 24 24 18 18 57*0 c a 9 4 2 1 0 0 30 50 90 20 40 80 0 7*80 ff 7*0 ff 7*1 ff 3 f 3f ff
  //   ff 3f f 3 c0 f0 fc ff ff fc f0 c0 3 c 30 c0 c0 30 c 3 c0 30 c 3 3 c 30 c0 20*0 f 8 8 8 4*0 ff 7*0 f0
  //   10 10 10 8*8 44 48 50 60 4*0 8*10 8 8 8 f 7*0 ff 4*0 10 10 10 f0 5*0 18 24 42 24 18 4*0 18 76 24 18
  //   5*0 2a 22 2 4*0 2 4c 30 7*0 42 3c 14*0 4*f 4*0 4*f0 4*0 4*ff 4*f 4*0 12*f 4*f0 4*f 4*ff 4*f0 4*0
  //   4*f0 4*f 12*f0 8*ff 4*0 4*ff 4*f 4*ff 4*f0 8*ff 8*0 8*3 8*c 8*f 8*30 8*33 8*3c 8*3f 8*c0 8*c3 8*cc
  //   8*cf 8*f0 8*f3 8*fc 8*ff
  //   CharROM
  //   Data ready by /CLK mid-cycle for VDP
  //   CharROM Output
  //   U55
  //   CharROM
  //   Bypass MUX
  //   U54
  //   Row of 32
  //   contents of rom_2 (hex, n*v repeats v):
  //   78 d8 a9 10 85 de a2 0 86 cc 20 81 fe a0 0 20 1e fd a6 dd ca ca 86 cd 20 ec c7 a0 1c 20 1e fd 78 d8
  //   20 8e ff 20 90 c8 a0 3a 20 1e fd a2 ff 9a e8 86 9a a5 9a f0 e a5 98 85 cc a5 99 85 cd 20 ec c7 20 f8
  //   c7 20 8 fe 20 52 fd a0 0 84 5e 84 5f 20 ed c6 c9 0 f0 d5 a5 9a d0 17 20 2b c3 b0 12 a2 37 20 58 c3
  //   b0 27 20 a8 c0 a9 1 20 a1 c8 4c c5 c9 20 ed c6 c9 0 f0 28 20 a8 c0 20 8 c9 18 a5 98 65 9a 85 98 90
  //   aa e6 99 f0 a0 d0 a4 20 95 c0 4c 33 c0 29 f aa a9 c8 48 bd 5a c4 48 4c ed c6 20 55 c8 4c 2d c0 20 d2
  //   c0 a9 3a 20 4a c3 f0 f6 20 ca c0 4c 71 c1 a5 cd d0 9 a5 cc c9 a b0 3 4c d0 c7 a0 c1 4c e7 c4 a2 1b
  //   20 58 c3 b0 3f 60 a2 c6 20 62 c3 b0 f a9 22 20 4a c3 d0 d5 a9 9c 20 d0 c7 4c 82 c2 29 3f aa bd a6 c4
  //   a2 c1 85 c0 86 c1 6c c0 10*0 20 ca c7 20 2a c2 a2 0 20 58 c3 90 c5 4c 14 c3 a9 c9 20 d0 c7 68 68 20
  //   df c7 20 ca c7 4c 14 c3 20 3a c2 a2 5 20 58 c3 90 47 20 2a c2 a2 8 20 58 c3 90 53 4c 2a c2 20 e7 c2
  //   a5 9b c9 1 f0 31 60 a9 23 20 39 c3 20 fe cc 90 26 4c b8 c0 a2 d 20 58 c3 90 1c 20 42 c2 a9 28 20 4a
  //   c3 d0 8 20 42 c2 20 48 c3 f0 f8 a9 3d 20 4a c3 d0 19 4c e0 c0 a0 8c 4c e7 c4 20 e7 c2 a9 3d 20 39 c3
  //   20 82 c2 a5 9b c5 9c d0 5b 60 20 2a c2 20 37 c3 20 2a c2 20 37 c3 4c 2a c2 20 88 c1 20 9d c1 20 48
  //   c3 d0 e5 4c 2a c2 20 e7 c2 a9 24 20 4a c3 d0 3 20 d0 c7 a9 28 20 39 c3 4c 6 c3 20 ca c7 20 99 c3 4c
  //   df c7 20 ca c7 a9 0 85 9d 20 e7 c2 e6 9d 20 48 c3 f0 f6 a9 9d 4c e4 c7 20 41 c1 20 37 c3 4c 32 c2 a0
  //   b6 4c e7 c4 a6 90 20 57 c3 20 ca c0 20 e7 c2 4c e7 c1 20 c8 c3 4c e7 c1 a2 9b 20 57 c3 a2 10 20 58
  //   c3 b0 9 20 ca c0 20 82 c2 4c fb c1 29 bf 20 d0 c7 a9 28 20 4a c3 c9 ba d0 6 20 2a c2 20 37 c3 20 2a
  //   c2 4c fb c1 20 82 c2 a5 9b d0 b1 60 20 82 c2 a5 9b f0 a9 60 20 e7 c2 a5 9b d0 a1 60 20 e7 c2 a5 9b
  //   f0 99 60 e6 9c 60 20 2a c2 20 48 c3 90 52 4c 2a c2 4c 32 c2 20 4a c2 20 32 c2 4c 50 c2 20 5b c2 4c
  //   50 c2 20 4a c2 4c 2a c2 4c 46 c1 20 82 c2 a5 9c c9 1 f0 3 20 32 c2 4c 32 c2 a9 0 85 9c a2 6c 20 57
  //   c3 20 ed c6 aa 20 f7 c6 90 16 8a 20 c4 c7 90 28 b0 b a9 bb 20 d0 c7 20 c8 c3 4c c2 c2 4c 71 c1 a2 c7
  //   20 62 c3 b0 6 20 e7 c2 4c c2 c2 29 3f aa bd c9 c4 a2 c2 4c f0 c0 a2 75 20 57 c3 a2 20 20 58 c3 60 a2
  //   88 20 57 c3 a9 ac 20 d0 c7 4c 86 c2 a2 8b 20 57 c3 a9 aa 20 d0 c7 4c 86 c2 a9 0 85 9b 20 a8 c3 90 b7
  //   a9 24 20 4a c3 d0 5 20 d0 c7 e6 9b a9 28 20 4a c3 d0 10 20 d0 c7 20 2a c2 20 48 c3 f0 f8 a9 29 4c 39
  //   c3 60 20 fe cc 90 f a9 cc 20 d0 c7 a5 cc 20 d0 c7 a5 cd 4c d0 c7 4c d2 c0 20 fe cc a5 cc 85 98 a5 cd
  //   85 99 60 a9 2c 85 c6 20 ed c6 c5 c6 d0 1 60 a5 c6 4c ed c4 a9 2c 85 c6 20 ed c6 c5 c6 d0 3 c8 a2 0
  //   60 60 20 ed c6 a9 c4 85 c1 8a d0 11 20 ed c6 20 f7 c6 b0 2b 86 c1 aa a9 0 85 c0 b5 c0 85 c0 a2 0 84
  //   c6 88 c6 c0 c8 e6 c0 a1 c0 30 14 d9 0 1 f0 f4 e6 c0 a1 c0 10 fa e6 c0 a4 c6 a 30 e4 18 60 38 60 20
  //   ed c6 b9 0 1 f0 6 c8 20 d0 c7 10 f5 60 20 ed c6 aa 20 f7 c6 b0 16 8a 20 d0 c7 b9 0 1 c8 aa 20 f7 c6
  //   90 f2 8a 20 c4 c7 90 ec 88 18 60 88 d0 3 20 d0 c7 c8 b9 0 1 f0 b c9 22 d0 f3 c8 d9 0 1 f0 ed 60 a9
  //   22 4c ed c4 28*0 54 48 45 4e 80 54 4f 80 53 54 45 50 80 46 4e 80 53 50 43 f8 54 41 42 f9 41 54 fa 45
  //   4c 53 45 c9 41 4e 44 f0 4f 52 f1 45 4f 52 f2 44 49 56 f3 4d 4f 44 b4 4e 4f 54 b5 4c 49 53 54 c0 52
  //   55 4e c1 41 55 54 4f c2 41 52 54 c3 53 41 56 45 c4 44 45 4c c5 4e 45 57 c6 4f 4c 44 87 0 84 5f 2 1
  //   34 8f 9f 87 f5 e7 fb 86 9c cd da 17 e7 2d a1 2b 4 28 a0 22 5 84 2b a2 2d a3 2a a4 2f a5 5e a6 3d a8
  //   29 9 3e 6 3c 7 84 3d ad 84 3d ab 3e a9 84 22 1 2c 80 3b 80 3a 40 0 40 82 2c 80 3b 81 27 82 3a 40 0
  //   40 83 87 87 87 41 87 ba 8e a5 4e 17 87 20 94 94 0 e7 76 df 8e 94 37 8e d9 88 fb 8e 8e c3 87 94 87 ba
  //   97 94 94 6*4c 9*55 4d 58 58 58 4a 73 5b 5b 5b 64 6a 6a 70 70 41 20 1e fd 4c 2d c0 48 a0 83 20 24 fd
  //   68 20 66 fd 20 52 fd 4c 2d c0 0 0 0 1b 92 93 94 95 96 90 d d 46 72 6f 6e 74 69 65 72 20 42 41 53 49
  //   43 20 31 2e 30 d 1d 20 62 79 74 65 73 20 66 72 65 65 d 54 79 70 65 20 41 52 54 20 74 6f 20 64 72 61
  //   77 d 5 52 65 61 64 79 9 53 65 61 72 63 68 69 6e 67 7 4c 6f 61 64 69 6e 67 20 41 52 54 20 ac ad ae af
  //   20 6d 6f 76 65 20 47 52 41 20 64 72 61 77 20 43 4f 4c 20 63 6f 6c 6f 72 4 50 4c 41 59 4 53 54 4f 50
  //   5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
  //   U45-U57 (+U39)
  //   U39 8-bit Shift Register
  //   U53
  //   VDP Latch
  //   Latched at /CLK
  //   VDP Latch Output
  //   VDP read during first half of CLK
  //   Data from memory latched at /CLK
  //   5 Pixel Pipe + 7 Color/2bpp
  //   U45 Dual D-FF 74LS74 (Delay/Clocking)
  //   U53 8-bit Register 74LS273 (VDP Latch)
  //   U54 Quad 1-of-2 MUX 74LS157 (Char Bypass MUX)
  //   U55 Quad 1-of-2 MUX 74LS157 (Char Bypass MUX)
  //   U46 Dual 1-of-4 74LS153 (Palette MUX)
  //   U47 Dual 1-of-4 74LS153 (Palette MUX)
  //   U48 4-bit DFF with Clear 74LS175 (FG)
  //   U49 4-bit DFF with Clear 74LS175 (BG)
  //   U50 Quad 1-of-2 MUX 74LS157 (FG)
  //   U51 Quad 1-of-2 MUX 74LS157 (BG)
  //   U52 8-bit Register 74LS273 (Color 2/3)
  //   U56 Triple 3-AND 74LS11 (Color Decode)
  //   U57 Quad 2-AND 74LS08 (Color Decode)
  //   U58 Quad 2-OR 74LS32 (Color Decode)
  //   U59 Hex NOT 74LS04 (Color Decode)
  //   Data Bus
  //   Latch data at /CLK for VDP
  //   Video Out
  //   nWPal
  //   PCLK
  //   HSync
  //   Burst
  //   VSync
  //   Color
  //   Pixel Color
  //   VSync
  //   VSync
  //   HSync
  //   Vpos
  //   Hpos
  //   PCLK / Hsync
  //   Hsync / Vsync
  //   Most home computers/consoles use 0 IRE
  //   for both Black and Blanking level
endmodule

// DBUS
module PSG (
  input  HSync,
  input  nPHI2,
  input  nWR,
  input  [7:0] DBUS,
  output SND
);

  wire CounterHi_pin1, CounterHi_pin7, CounterHi_pin9, CounterHi_pin15, CounterLo_pin1, CounterLo_pin7,
       FreqLatch_pin2, FreqLatch_pin5, FreqLatch_pin6, FreqLatch_pin9, FreqLatch_pin12, FreqLatch_pin15,
       FreqLatch_pin16, FreqLatch_pin19;

  _74377 #(.ShowInternalStructure("true")) FreqLatch (
    .pin1(nWR), .pin2(FreqLatch_pin2), .pin3(DBUS[0]), .pin4(DBUS[1]), .pin5(FreqLatch_pin5),
    .pin6(FreqLatch_pin6), .pin7(DBUS[2]), .pin8(DBUS[3]), .pin9(FreqLatch_pin9), .pin19(FreqLatch_pin19),
    .pin18(DBUS[7]), .pin17(DBUS[6]), .pin16(FreqLatch_pin16), .pin15(FreqLatch_pin15), .pin14(DBUS[5]),
    .pin13(DBUS[4]), .pin12(FreqLatch_pin12), .pin11(nPHI2));
  _74161 #(.ShowInternalStructure("true")) CounterHi (
    .pin1(CounterHi_pin1), .pin2(HSync), .pin3(FreqLatch_pin12), .pin4(FreqLatch_pin15),
    .pin5(FreqLatch_pin16), .pin6(FreqLatch_pin19), .pin7(CounterHi_pin7), .pin15(CounterHi_pin15),
    .pin10(CounterHi_pin7), .pin9(CounterHi_pin9));  // open: pin14, pin13, pin12, pin11
  _74161 #(.ShowInternalStructure("true")) CounterLo (
    .pin1(CounterLo_pin1), .pin2(HSync), .pin3(FreqLatch_pin2), .pin4(FreqLatch_pin5), .pin5(FreqLatch_pin6),
    .pin6(FreqLatch_pin9), .pin7(CounterLo_pin7), .pin15(CounterHi_pin7), .pin10(CounterLo_pin7),
    .pin9(CounterHi_pin9));  // open: pin14, pin13, pin12, pin11
  not not_1 (CounterHi_pin9, CounterHi_pin15);
  T_Flip_Flop t_ff_1 (.clk(HSync), .T(CounterHi_pin15), .Q(SND));  // open: Qn, preset, reset
  LED led_1 (.in(SND));
  // also tied to VCC on the sheet: {CounterHi_pin1, CounterLo_pin1, CounterLo_pin7}

  // Notes on the sheet:
  //   nWR: initial=0x1
  //   DBUS: initial=0x80
  //   Note: if using 374, NOR nWR with nPHI2
  //   IO address decode
  //   Rising Edge as PHI2 falls
  //   74LS374 ?
  //   15720 Hz
  //   DIV 2
endmodule

module SN74LS298 (
  input  WS,
  input  A1,
  input  B1,
  input  C1,
  input  D1,
  input  A2,
  input  B2,
  input  C2,
  input  D2,
  input  CLK,
  output QA,
  output QB,
  output QC,
  output QD
);

  wire n74157_1_pin4, n74157_1_pin7, n74157_1_pin9, n74157_1_pin12, n74157_1_pin15, n74175_1_pin1;

  _74157 #(.ShowInternalStructure("true")) u_74157_1 (
    .pin1(WS), .pin2(A1), .pin3(A2), .pin4(n74157_1_pin4), .pin5(B1), .pin6(B2), .pin7(n74157_1_pin7),
    .pin15(n74157_1_pin15), .pin14(D1), .pin13(D2), .pin12(n74157_1_pin12), .pin11(C1), .pin10(C2),
    .pin9(n74157_1_pin9));
  _74175 #(.ShowInternalStructure("true")) u_74175_1 (
    .pin1(n74175_1_pin1), .pin2(QA), .pin4(n74157_1_pin4), .pin5(n74157_1_pin7), .pin7(QB), .pin15(QD),
    .pin13(n74157_1_pin12), .pin12(n74157_1_pin9), .pin10(QC), .pin9(CLK));  // open: pin3, pin6, pin14, pin11
  // also tied to GND on the sheet: n74157_1_pin15
  // also tied to VCC on the sheet: n74175_1_pin1

  // Notes on the sheet:
  //   74LS175
endmodule

// 555
module Timer_555 (
  input  [7:0] Count,
  input  Trigger,
  output DOut
);

  wire clock_1_out, counter_1_carry, j_k_ff_1_q, not_1_out;

  Clock clock_1 (.out(clock_1_out));
  not not_1 (not_1_out, Trigger);
  J_K_Flip_Flop j_k_ff_1 (
    .J(1'b0), .clk(clock_1_out), .K(1'b1), .Q(j_k_ff_1_q), .preset(not_1_out));  // open: Qn, reset
  Counter counter_1 (
    .load(j_k_ff_1_q), .D(Count), .count(DOut), .carry(counter_1_carry), .clk(clock_1_out));  // open: Q, up, clr
  J_K_Flip_Flop j_k_ff_2 (
    .J(1'b0), .clk(clock_1_out), .K(counter_1_carry), .Q(DOut), .preset(j_k_ff_1_q));  // open: Qn, reset

  // Notes on the sheet:
  //   555 triggers
  //   on falling edge
  //   14.31818 MHz
  //   pulse
endmodule

// 393
module SN74LS393 (
  input  nCLK1,
  input  CLR1,
  input  nCLK2,
  input  CLR2,
  output QA,
  output QB,
  output QC,
  output QD,
  output QE,
  output QF,
  output QG,
  output QH
);

  wire not_1_out, not_2_out, t_ff_1_qn, t_ff_2_qn, t_ff_3_qn, t_ff_5_qn, t_ff_6_qn, t_ff_7_qn;

  not not_1 (not_1_out, nCLK1);
  not not_2 (not_2_out, nCLK2);
  T_Flip_Flop t_ff_1 (.clk(not_1_out), .T(1'b1), .Q(QA), .Qn(t_ff_1_qn), .reset(CLR1));  // open: preset
  T_Flip_Flop t_ff_2 (.clk(t_ff_1_qn), .T(1'b1), .Q(QB), .Qn(t_ff_2_qn), .reset(CLR1));  // open: preset
  T_Flip_Flop t_ff_3 (.clk(t_ff_2_qn), .T(1'b1), .Q(QC), .Qn(t_ff_3_qn), .reset(CLR1));  // open: preset
  T_Flip_Flop t_ff_4 (.clk(t_ff_3_qn), .T(1'b1), .Q(QD), .reset(CLR1));  // open: Qn, preset
  T_Flip_Flop t_ff_5 (.clk(not_2_out), .T(1'b1), .Q(QE), .Qn(t_ff_5_qn), .preset(1'b0), .reset(CLR2));
  T_Flip_Flop t_ff_6 (.clk(t_ff_5_qn), .T(1'b1), .Q(QF), .Qn(t_ff_6_qn), .preset(1'b0), .reset(CLR2));
  T_Flip_Flop t_ff_7 (.clk(t_ff_6_qn), .T(1'b1), .Q(QG), .Qn(t_ff_7_qn), .preset(1'b0), .reset(CLR2));
  T_Flip_Flop t_ff_8 (.clk(t_ff_7_qn), .T(1'b1), .Q(QH), .preset(1'b0), .reset(CLR2));  // open: Qn
endmodule

// 170
module SN74LS170 (
  input  D1,
  input  D2,
  input  D3,
  input  D4,
  input  RB,
  input  RA,
  input  nGR,
  input  nGW,
  input  WB,
  input  WA,
  output Q1,
  output Q2,
  output Q3,
  output Q4
);

  wire and_1_out, and_2_out, and_3_out, and_4_out, and_5_out, and_6_out, and_7_out, and_8_out, and_9_out,
       and_10_out, and_11_out, and_12_out, and_13_out, and_14_out, and_15_out, and_16_out, and_17_out,
       and_18_out, and_19_out, and_20_out, and_21_out, and_22_out, and_23_out, and_24_out, d_ff_1_q,
       d_ff_2_q, d_ff_3_q, d_ff_4_q, d_ff_5_q, d_ff_6_q, d_ff_7_q, d_ff_8_q, d_ff_9_q, d_ff_10_q, d_ff_11_q,
       d_ff_12_q, d_ff_13_q, d_ff_14_q, d_ff_15_q, d_ff_16_q, not_1_out, not_2_out, not_3_out, not_4_out,
       not_5_out, not_6_out, not_7_out, not_8_out, not_9_out;

  not not_1 (not_1_out, D1);
  not not_2 (not_2_out, D2);
  not not_3 (not_3_out, D3);
  not not_4 (not_4_out, D4);
  and and_1 (and_1_out, not_7_out, and_3_out);
  and and_2 (and_2_out, ~nGW, ~not_5_out);  // AND_Gate
  D_Flip_Flop #(.trigger("high")) d_ff_1 (.clk(and_1_out), .D(not_1_out), .Q(d_ff_1_q));  // open: Qn, preset, reset
  D_Flip_Flop #(.trigger("high")) d_ff_2 (.clk(and_1_out), .D(not_2_out), .Q(d_ff_2_q));  // open: Qn, preset, reset
  D_Flip_Flop #(.trigger("high")) d_ff_3 (.clk(and_1_out), .D(not_3_out), .Q(d_ff_3_q));  // open: Qn, preset, reset
  D_Flip_Flop #(.trigger("high")) d_ff_4 (.clk(and_1_out), .D(not_4_out), .Q(d_ff_4_q));  // open: Qn, preset, reset
  and and_3 (and_3_out, ~nGW, not_5_out);  // AND_Gate
  not not_5 (not_5_out, WB);
  and and_4 (and_4_out, and_3_out, not_6_out);
  not not_6 (not_6_out, not_7_out);
  not not_7 (not_7_out, WA);
  D_Flip_Flop #(.trigger("high")) d_ff_5 (.clk(and_4_out), .D(not_1_out), .Q(d_ff_5_q));  // open: Qn, preset, reset
  D_Flip_Flop #(.trigger("high")) d_ff_6 (.clk(and_4_out), .D(not_2_out), .Q(d_ff_6_q));  // open: Qn, preset, reset
  D_Flip_Flop #(.trigger("high")) d_ff_7 (.clk(and_4_out), .D(not_3_out), .Q(d_ff_7_q));  // open: Qn, preset, reset
  D_Flip_Flop #(.trigger("high")) d_ff_8 (.clk(and_4_out), .D(not_4_out), .Q(d_ff_8_q));  // open: Qn, preset, reset
  and and_5 (and_5_out, and_2_out, not_7_out);
  D_Flip_Flop #(.trigger("high")) d_ff_9 (.clk(and_5_out), .D(not_1_out), .Q(d_ff_9_q));  // open: Qn, preset, reset
  D_Flip_Flop #(.trigger("high")) d_ff_10 (.clk(and_5_out), .D(not_2_out), .Q(d_ff_10_q));  // open: Qn, preset, reset
  D_Flip_Flop #(.trigger("high")) d_ff_11 (.clk(and_5_out), .D(not_3_out), .Q(d_ff_11_q));  // open: Qn, preset, reset
  D_Flip_Flop #(.trigger("high")) d_ff_12 (.clk(and_5_out), .D(not_4_out), .Q(d_ff_12_q));  // open: Qn, preset, reset
  and and_6 (and_6_out, and_2_out, not_6_out);
  D_Flip_Flop #(.trigger("high")) d_ff_13 (.clk(and_6_out), .D(not_1_out), .Q(d_ff_13_q));  // open: Qn, preset, reset
  D_Flip_Flop #(.trigger("high")) d_ff_14 (.clk(and_6_out), .D(not_2_out), .Q(d_ff_14_q));  // open: Qn, preset, reset
  D_Flip_Flop #(.trigger("high")) d_ff_15 (.clk(and_6_out), .D(not_3_out), .Q(d_ff_15_q));  // open: Qn, preset, reset
  D_Flip_Flop #(.trigger("high")) d_ff_16 (.clk(and_6_out), .D(not_4_out), .Q(d_ff_16_q));  // open: Qn, preset, reset
  not not_8 (not_8_out, not_9_out);
  and and_7 (and_7_out, ~nGR, ~and_8_out);  // AND_Gate
  not not_9 (not_9_out, RB);
  and and_8 (and_8_out, ~nGR, ~RA);  // AND_Gate
  and and_9 (and_9_out, d_ff_1_q, not_9_out, and_8_out);
  and and_10 (and_10_out, d_ff_5_q, not_9_out, and_7_out);
  and and_11 (and_11_out, d_ff_9_q, not_8_out, and_8_out);
  and and_12 (and_12_out, d_ff_13_q, not_8_out, and_7_out);
  and and_13 (and_13_out, d_ff_2_q, not_9_out, and_8_out);
  and and_14 (and_14_out, d_ff_6_q, not_9_out, and_7_out);
  and and_15 (and_15_out, d_ff_10_q, not_8_out, and_8_out);
  and and_16 (and_16_out, d_ff_14_q, not_8_out, and_7_out);
  and and_17 (and_17_out, d_ff_3_q, not_9_out, and_8_out);
  and and_18 (and_18_out, d_ff_7_q, not_9_out, and_7_out);
  and and_19 (and_19_out, d_ff_11_q, not_8_out, and_8_out);
  and and_20 (and_20_out, d_ff_15_q, not_8_out, and_7_out);
  and and_21 (and_21_out, d_ff_4_q, not_9_out, and_8_out);
  and and_22 (and_22_out, d_ff_8_q, not_9_out, and_7_out);
  and and_23 (and_23_out, d_ff_12_q, not_8_out, and_8_out);
  and and_24 (and_24_out, d_ff_16_q, not_8_out, and_7_out);
  nor nor_1 (Q1, and_9_out, and_10_out, and_11_out, and_12_out);
  nor nor_2 (Q2, and_13_out, and_14_out, and_15_out, and_16_out);
  nor nor_3 (Q3, and_17_out, and_18_out, and_19_out, and_20_out);
  nor nor_4 (Q4, and_21_out, and_22_out, and_23_out, and_24_out);
endmodule

module Test_170 (
);

  wire [3:0] sn74ls170_1_q1;

  SN74LS170 sn74ls170_1 (
    .D1(1'b1), .D2(1'b0), .D3(1'b1), .D4(1'b1), .RB(1'b1), .RA(1'b1), .nGR(1'b0), .nGW(1'b1), .WB(1'b1),
    .WA(1'b1), .Q1(sn74ls170_1_q1[0]), .Q2(sn74ls170_1_q1[1]), .Q3(sn74ls170_1_q1[2]), .Q4(sn74ls170_1_q1[3]));
  // Probe on sn74ls170_1_q1

  // Notes on the sheet:
  //   Rmux
  //   Din
  //   nRD
  //   nWR
  //   Wmux
endmodule
