// Logisim project HCountOld.circ as structural Verilog: 2 circuits, main circuit main
module main (
);

  wire and_1_out, and_2_out, and_3_out, and_4_out, and_5_out, and_6_out, and_7_out, and_9_out, and_10_out,
       and_11_out, and_12_out, and_13_out, and_14_out, and_16_out, and_17_out, and_18_out, clock_1_out,
       d_ff_1_q, d_ff_2_q, j_k_ff_3_q, j_k_ff_5_q, j_k_ff_6_q, j_k_ff_7_q, j_k_ff_7_qn, j_k_ff_8_q,
       n74138_1_pin9, n74138_1_pin11, n74138_1_pin12, n74138_1_pin15, n74153_1_pin1, n74153_1_pin2,
       n74153_1_pin3, n74153_1_pin4, n74153_1_pin5, n74153_1_pin6, n74153_1_pin7, n74153_1_pin9,
       n74153_1_pin10, n74153_1_pin11, n74153_1_pin12, n74153_1_pin13, n74153_1_pin15, n74153_2_pin1,
       n74153_2_pin3, n74153_2_pin4, n74153_2_pin5, n74153_2_pin6, n74153_2_pin7, n74153_2_pin9,
       n74153_2_pin10, n74153_2_pin11, n74153_2_pin12, n74153_2_pin13, n74153_2_pin15, n74157_1_pin2,
       n74157_1_pin3, n74157_1_pin5, n74157_1_pin6, n74157_1_pin10, n74157_1_pin11, n74157_1_pin13,
       n74157_1_pin14, n74157_1_pin15, n74161_1_pin1, n74161_1_pin3, n74161_1_pin11, n74161_1_pin14,
       n74161_1_pin15, n74161_2_pin1, n74161_2_pin2, n74161_2_pin3, n74161_2_pin4, n74161_2_pin5,
       n74161_2_pin6, n74161_2_pin7, n74161_2_pin9, n74161_3_pin1, n74161_3_pin3, n74161_3_pin4,
       n74161_3_pin5, n74161_3_pin6, n74161_3_pin7, n74161_4_pin1, n74161_4_pin2, n74161_4_pin3,
       n74161_4_pin4, n74161_4_pin5, n74161_4_pin6, n74161_4_pin7, n74161_4_pin9, n74161_4_pin15,
       n74161_5_pin1, n74161_5_pin3, n74161_5_pin4, n74161_5_pin5, n74161_5_pin6, n74161_5_pin7,
       n74166_1_pin1, n74166_1_pin2, n74166_1_pin3, n74166_1_pin4, n74166_1_pin5, n74166_1_pin6,
       n74166_1_pin7, n74166_1_pin9, n74166_1_pin10, n74166_1_pin11, n74166_1_pin12, n74166_1_pin13,
       n74166_1_pin14, n74273_1_pin1, n74273_1_pin3, n74273_1_pin4, n74273_1_pin7, n74273_1_pin8,
       n74273_1_pin11, n74273_1_pin13, n74273_1_pin14, n74273_1_pin17, n74273_1_pin18, n74273_2_pin1,
       n74273_2_pin3, n74273_2_pin4, n74273_2_pin7, n74273_2_pin8, n74273_2_pin13, n74273_2_pin14,
       n74273_2_pin17, n74273_2_pin18, not_2_out, not_5_out, not_6_out, not_7_out, not_8_out, not_9_out,
       not_10_out, not_11_out, not_12_out, not_13_out, not_14_out, not_16_out, or_1_out;
  wire [3:0] n74157_1_pin4;
  wire [7:0] multiplexer_1_out, multiplexer_3_out, multiplexer_4_out, multiplexer_5_out, rgb_video_1_p6;
  wire [8:0] n74161_1_pin13, n74161_5_pin14;

  Clock clock_1 (.out(clock_1_out));
  _74161 #(.ShowInternalStructure("true")) u_74161_1 (
    .pin1(n74161_1_pin1), .pin2(clock_1_out), .pin3(n74161_1_pin3), .pin4(n74161_1_pin3),
    .pin5(n74161_1_pin3), .pin6(n74161_1_pin3), .pin7(n74161_1_pin3), .pin15(n74161_1_pin15),
    .pin14(n74161_1_pin14), .pin13(n74161_1_pin13[0]), .pin12(n74161_1_pin13[1]), .pin11(n74161_1_pin11),
    .pin10(n74161_1_pin3), .pin9(n74161_1_pin3));
  _74161 #(.ShowInternalStructure("true")) u_74161_2 (
    .pin1(n74161_2_pin1), .pin2(n74161_2_pin2), .pin3(n74161_2_pin3), .pin4(n74161_2_pin4),
    .pin5(n74161_2_pin5), .pin6(n74161_2_pin6), .pin7(n74161_2_pin7), .pin14(n74161_1_pin13[7]),
    .pin13(n74161_1_pin13[8]), .pin10(n74161_2_pin7), .pin9(n74161_2_pin9));  // open: pin15, pin12, pin11
  _74161 #(.ShowInternalStructure("true")) u_74161_3 (
    .pin1(n74161_3_pin1), .pin2(n74161_2_pin2), .pin3(n74161_3_pin3), .pin4(n74161_3_pin4),
    .pin5(n74161_3_pin5), .pin6(n74161_3_pin6), .pin7(n74161_3_pin7), .pin15(n74161_2_pin7),
    .pin14(n74161_1_pin13[3]), .pin13(n74161_1_pin13[4]), .pin12(n74161_1_pin13[5]),
    .pin11(n74161_1_pin13[6]), .pin10(n74161_3_pin7), .pin9(n74161_2_pin9));
  _74161 #(.ShowInternalStructure("true")) u_74161_4 (
    .pin1(n74161_4_pin1), .pin2(n74161_4_pin2), .pin3(n74161_4_pin3), .pin4(n74161_4_pin4),
    .pin5(n74161_4_pin5), .pin6(n74161_4_pin6), .pin7(n74161_4_pin7), .pin15(n74161_4_pin15),
    .pin14(n74161_5_pin14[4]), .pin13(n74161_5_pin14[5]), .pin12(n74161_5_pin14[6]),
    .pin11(n74161_5_pin14[7]), .pin10(n74161_4_pin7), .pin9(n74161_4_pin9));
  _74161 #(.ShowInternalStructure("true")) u_74161_5 (
    .pin1(n74161_5_pin1), .pin2(n74161_4_pin2), .pin3(n74161_5_pin3), .pin4(n74161_5_pin4),
    .pin5(n74161_5_pin5), .pin6(n74161_5_pin6), .pin7(n74161_5_pin7), .pin15(n74161_4_pin7),
    .pin14(n74161_5_pin14[0]), .pin13(n74161_5_pin14[1]), .pin12(n74161_5_pin14[2]),
    .pin11(n74161_5_pin14[3]), .pin10(n74161_5_pin7), .pin9(n74161_4_pin9));
  not not_1 (n74161_2_pin2, not_2_out);
  J_K_Flip_Flop j_k_ff_1 (
    .J(n74161_4_pin15), .clk(n74161_4_pin2), .K(and_2_out), .Q(n74161_5_pin14[8]));  // open: Qn, preset, reset
  not not_2 (not_2_out, n74161_1_pin11);
  and and_1 (and_1_out, n74161_1_pin13[7], n74161_1_pin13[8], n74161_1_pin13[6]);
  not not_3 (n74161_2_pin9, and_1_out);
  and and_2 (and_2_out, n74161_5_pin14[8], and_3_out);
  not not_4 (n74161_4_pin9, and_2_out);
  not not_5 (not_5_out, n74161_1_pin13[7]);
  not not_6 (not_6_out, n74161_5_pin14[7]);
  and and_3 (and_3_out, n74161_5_pin14[2], n74161_5_pin14[0]);
  and and_4 (and_4_out, n74161_1_pin13[8], not_5_out, n74161_1_pin13[6]);
  and and_5 (and_5_out, n74161_1_pin13[7], n74161_1_pin13[8]);
  D_Flip_Flop d_ff_1 (.clk(n74161_4_pin2), .D(and_2_out), .Q(d_ff_1_q));  // open: Qn, preset, reset
  J_K_Flip_Flop j_k_ff_2 ();  // open: J, clk, K, Q, Qn, preset, reset
  and and_6 (and_6_out, and_5_out, n74161_1_pin13[4]);
  and and_7 (and_7_out, n74161_1_pin13[3], and_5_out);
  _74138 #(.ShowInternalStructure("true")) u_74138_1 (
    .pin1(n74161_5_pin14[3]), .pin2(n74161_5_pin14[4]), .pin3(n74161_5_pin14[5]), .pin4(n74161_5_pin14[8]),
    .pin5(not_6_out), .pin6(n74161_5_pin14[6]), .pin15(n74138_1_pin15), .pin12(n74138_1_pin12),
    .pin11(n74138_1_pin11), .pin9(n74138_1_pin9));  // open: pin7, pin14, pin13, pin10
  // AND_Gate and_8 is placed but not wired
  not not_7 (not_7_out, and_9_out);
  and and_9 (and_9_out, and_4_out, n74161_1_pin13[5], n74161_1_pin13[4]);
  and and_10 (and_10_out, and_4_out, n74161_2_pin7);
  not not_8 (not_8_out, n74138_1_pin12);
  not not_9 (not_9_out, n74138_1_pin11);
  not not_10 (not_10_out, n74138_1_pin9);
  not not_11 (not_11_out, n74138_1_pin15);
  not not_12 (not_12_out, n74161_1_pin11);
  and and_11 (and_11_out, and_4_out, not_7_out, n74161_1_pin13[4]);
  not not_13 (not_13_out, n74161_1_pin13[8]);
  // Probe on not_13_out
  and and_12 (and_12_out, not_8_out, and_3_out);
  not not_14 (not_14_out, not_12_out);
  J_K_Flip_Flop j_k_ff_3 (.J(and_4_out), .clk(not_14_out), .K(and_6_out), .Q(j_k_ff_3_q));  // open: Qn, preset, reset
  J_K_Flip_Flop j_k_ff_4 (
    .J(and_11_out), .clk(not_14_out), .K(and_9_out), .Q(n74161_4_pin2));  // open: Qn, preset, reset
  D_Flip_Flop d_ff_2 (.clk(not_14_out), .D(not_13_out), .Q(d_ff_2_q));  // open: Qn, preset, reset
  and and_13 (and_13_out, j_k_ff_5_q, j_k_ff_5_q, j_k_ff_7_qn);
  J_K_Flip_Flop j_k_ff_5 (.J(and_10_out), .clk(not_14_out), .K(and_7_out), .Q(j_k_ff_5_q));  // open: Qn, preset, reset
  J_K_Flip_Flop j_k_ff_6 (.J(and_12_out), .clk(not_14_out), .K(not_10_out), .Q(j_k_ff_6_q));  // open: Qn, preset, reset
  J_K_Flip_Flop j_k_ff_7 (
    .J(and_12_out), .clk(not_14_out), .K(not_9_out), .Q(j_k_ff_7_q), .Qn(j_k_ff_7_qn));  // open: preset, reset
  J_K_Flip_Flop j_k_ff_8 (.J(d_ff_1_q), .clk(not_14_out), .K(not_11_out), .Q(j_k_ff_8_q));  // open: Qn, preset, reset
  // Probe on j_k_ff_3_q
  not not_15 (n74161_1_pin13[2], n74161_1_pin11);
  // Probe on n74161_1_pin13
  and and_14 (and_14_out, d_ff_2_q, j_k_ff_8_q);
  // Probe on j_k_ff_6_q
  // Probe on n74161_5_pin14
  // RGB_Video #(.cursor("No Cursor"), .height(262), .scale(1), .width(458)) rgb_video_1: pin names not known; wires that end beside it: 1'b0, n74161_1_pin14, 1'b1, n74161_1_pin13, n74161_5_pin14, rgb_video_1_p6
  or or_1 (or_1_out, j_k_ff_3_q, j_k_ff_6_q);
  Multiplexer #(.width(8)) multiplexer_1 (
    .in0({8{1'b0}}), .in1({4'b0000, n74157_1_pin4}), .out(multiplexer_1_out), .sel(and_14_out));
  Multiplexer #(.width(8)) multiplexer_2 (.in0(multiplexer_3_out), .in1(8'hc), .out(rgb_video_1_p6), .sel(j_k_ff_7_q));
  Multiplexer #(.width(8)) multiplexer_3 (
    .in0(multiplexer_1_out), .in1(multiplexer_4_out), .out(multiplexer_3_out), .sel(or_1_out));
  Multiplexer #(.width(8)) multiplexer_4 (
    .in0(multiplexer_5_out), .in1(8'hb), .out(multiplexer_4_out), .sel(and_13_out));
  Multiplexer #(.width(8)) multiplexer_5 (.in0(8'h2b), .in1(8'hd), .out(multiplexer_5_out), .sel(n74161_4_pin2));
  // Probe on j_k_ff_7_q
  not not_16 (not_16_out, n74161_1_pin15);
  _74166 #(.ShowInternalStructure("true")) u_74166_1 (
    .pin1(n74166_1_pin1), .pin2(n74166_1_pin2), .pin3(n74166_1_pin3), .pin4(n74166_1_pin4),
    .pin5(n74166_1_pin5), .pin6(n74166_1_pin6), .pin7(n74166_1_pin7), .pin15(not_16_out),
    .pin14(n74166_1_pin14), .pin13(n74166_1_pin13), .pin12(n74166_1_pin12), .pin11(n74166_1_pin11),
    .pin10(n74166_1_pin10), .pin9(n74166_1_pin9));
  _74157 #(.ShowInternalStructure("true")) u_74157_1 (
    .pin1(n74166_1_pin13), .pin2(n74157_1_pin2), .pin3(n74157_1_pin3), .pin4(n74157_1_pin4[0]),
    .pin5(n74157_1_pin5), .pin6(n74157_1_pin6), .pin7(n74157_1_pin4[1]), .pin15(n74157_1_pin15),
    .pin14(n74157_1_pin14), .pin13(n74157_1_pin13), .pin12(n74157_1_pin4[3]), .pin11(n74157_1_pin11),
    .pin10(n74157_1_pin10), .pin9(n74157_1_pin4[2]));
  and and_15 (n74166_1_pin7, and_16_out, and_16_out);
  and and_16 (and_16_out, and_17_out, and_17_out);
  and and_17 (and_17_out, and_18_out, and_18_out);
  and and_18 (and_18_out, n74161_1_pin14, n74161_1_pin14);
  _74153 #(.ShowInternalStructure("true")) u_74153_1 (
    .pin1(n74153_1_pin1), .pin2(n74153_1_pin2), .pin3(n74153_1_pin3), .pin4(n74153_1_pin4),
    .pin5(n74153_1_pin5), .pin6(n74153_1_pin6), .pin7(n74153_1_pin7), .pin15(n74153_1_pin15),
    .pin14(n74153_1_pin2), .pin13(n74153_1_pin13), .pin12(n74153_1_pin12), .pin11(n74153_1_pin11),
    .pin10(n74153_1_pin10), .pin9(n74153_1_pin9));
  _74153 #(.ShowInternalStructure("true")) u_74153_2 (
    .pin1(n74153_2_pin1), .pin2(n74153_1_pin2), .pin3(n74153_2_pin3), .pin4(n74153_2_pin4),
    .pin5(n74153_2_pin5), .pin6(n74153_2_pin6), .pin7(n74153_2_pin7), .pin15(n74153_2_pin15),
    .pin14(n74153_1_pin2), .pin13(n74153_2_pin13), .pin12(n74153_2_pin12), .pin11(n74153_2_pin11),
    .pin10(n74153_2_pin10), .pin9(n74153_2_pin9));
  _74273 #(.ShowInternalStructure("true")) u_74273_1 (
    .pin1(n74273_1_pin1), .pin2(n74153_1_pin10), .pin3(n74273_1_pin3), .pin4(n74273_1_pin4),
    .pin5(n74153_1_pin6), .pin6(n74153_2_pin10), .pin7(n74273_1_pin7), .pin8(n74273_1_pin8),
    .pin9(n74153_2_pin6), .pin19(n74153_2_pin5), .pin18(n74273_1_pin18), .pin17(n74273_1_pin17),
    .pin16(n74153_2_pin11), .pin15(n74153_1_pin5), .pin14(n74273_1_pin14), .pin13(n74273_1_pin13),
    .pin12(n74153_1_pin11), .pin11(n74273_1_pin11));
  _74273 #(.ShowInternalStructure("true")) u_74273_2 (
    .pin1(n74273_2_pin1), .pin2(n74153_1_pin12), .pin3(n74273_2_pin3), .pin4(n74273_2_pin4),
    .pin5(n74153_1_pin4), .pin6(n74153_2_pin12), .pin7(n74273_2_pin7), .pin8(n74273_2_pin8),
    .pin9(n74153_2_pin4), .pin19(n74153_2_pin3), .pin18(n74273_2_pin18), .pin17(n74273_2_pin17),
    .pin16(n74153_2_pin13), .pin15(n74153_1_pin3), .pin14(n74273_2_pin14), .pin13(n74273_2_pin13),
    .pin12(n74153_1_pin13), .pin11(n74273_1_pin11));
  // also tied to GND on the sheet: {n74161_2_pin3, n74161_2_pin4, n74161_2_pin5, n74161_2_pin6, n74161_3_pin3, n74161_3_pin4, n74161_3_pin5, n74161_3_pin6, n74161_4_pin3, n74161_4_pin4, n74161_4_pin5, n74161_4_pin6, n74161_5_pin3, n74161_5_pin4, n74161_5_pin5, n74161_5_pin6, n74166_1_pin12, n74166_1_pin11, n74166_1_pin6, n74166_1_pin4, n74166_1_pin3, n74166_1_pin1, n74157_1_pin15, n74157_1_pin2, n74157_1_pin3, n74157_1_pin6}
  // also tied to VCC on the sheet: {n74161_1_pin1, n74161_2_pin1, n74161_3_pin1, n74161_3_pin7, n74161_4_pin1, n74161_5_pin1, n74161_5_pin7, n74161_1_pin3, n74166_1_pin14, n74166_1_pin9, n74166_1_pin10, n74166_1_pin5, n74166_1_pin2, n74157_1_pin14, n74157_1_pin13, n74157_1_pin5, n74157_1_pin11, n74157_1_pin10, n74153_1_pin15, n74153_2_pin15, n74153_1_pin1, n74153_2_pin1, n74273_1_pin1, n74273_2_pin1}

  // Notes on the sheet:
  //   CLK
  //   14.31818 MHz
  //   6-bit H-Count
  //   [0-56]
  //   U35
  //   U36
  //   9-bit V-Count
  //   U31B
  //   U40
  //   U41
  //   VScan= ~(d8+(d7•d6))
  //   U38A
  //   VBlank = 76~543 + 765~4~3 + 765~4~2
  //   VSync = VBL • ~(d4 + d3 + d2) • (d1 + d0)
  //   1 in 16
  //   7.15909 MHz
  //   3.579545 MHz
  //   1.7897725 MHz
  //   0.894886 MHz
  //   Clock Delay > Negative Edge Inverter
  //   RHC 56
  //   111xxx
  //   U32A
  //   RVC 261
  //   (100 000 101)
  //   RVC
  //   U43B
  //   U38F
  //   1x1
  //   U43A
  //   Work-around for incorrectly timed RCO output
  //   U38B
  //   U45A
  //   U30B
  //   Line Delay
  //   SHB 40
  //   101xxx
  //   U32B
  //   11xxxx
  //   U34A
  //   011
  //   RHB 50
  //   11xx1x
  //   U34B
  //   U46B
  //   RCB 49
  //   11xxx1
  //   U34C
  //   U42
  //   U37C
  //   RHS 46
  //   10111x
  //   U32C
  //   SCB 47
  //   101111
  //   U34D
  //   000
  //   011
  //   100
  //   110
  //   U45E
  //   N/A Negative Edge (74LS73)
  //   Negate Negative Edge (74LS73)
  //   Must be rising-edge for 8px delay
  //   U38C
  //   U38D
  //   Fetch
  //   U45B
  //   U45C
  //   U45D
  //   SHS 42
  //   101x1x
  //   U37A
  //   U31A
  //   Colorburst
  //   U43C
  //   1x1
  //   U45F
  //   U33 A
  //   HBlank
  //   U33B
  //   HSync
  //   U30A
  //   Visible
  //   U37B
  //   U44A
  //   VBlank
  //   U44B
  //   VSync
  //   U46A
  //   Visible
  //   N/A
  //   7.15909 MHz
  //   HCount
  //   Scan
  //   U43D
  //   HSync
  //   VSync
  //   Not VSync
  //   "74LS175"
  //   HBlank
  //   VBlank
  //   VCount
  //   HBlank
  //   Not HBlank
  //   VBlank
  //   Burst
  //   Colorburst
  //   Not Burst
  //   Not VBlank
  //   VSync
  //   HSync
  //   Not HSync
  //   Scan
  //   NotScan
  //   Not HBlank
  //   Many (most) home computers/consoles
  //   use 0 IRE for both Black and Blanking level
  //   (that would eliminate HBlank and VBlank)
  //   (saves 3 chips: 2xJK, 4xAND, 4xOR)
  //   HBlank
  //   Not VBlank
  //   --
  //   --
  //   VBlank
  //   Scan
  //   U38E
  //   VSync
  //   Not VSync
  //   VSync
  //   Not VSync
  //   HSync
  //   Not HSync
  //   NotScan
  //   74LS00 (3ns - 15ns)
  //   U39
  //   /CLK
  //   74LS08 (12 - 72ns)
  //   FG
  //   BG
  //   Red
  //   Yellow
endmodule

// DBUS
module PSG (
  input  HSync,
  input  nPHI2,
  input  nWR,
  input  [7:0] DBUS,
  output SND
);

  wire CounterHi_pin1, CounterHi_pin7, CounterHi_pin9, CounterHi_pin15, CounterLo_pin1, CounterLo_pin7,
       FreqLatch_pin2, FreqLatch_pin5, FreqLatch_pin6, FreqLatch_pin9, FreqLatch_pin12, FreqLatch_pin15,
       FreqLatch_pin16, FreqLatch_pin19;

  _74377 #(.ShowInternalStructure("true")) FreqLatch (
    .pin1(nWR), .pin2(FreqLatch_pin2), .pin3(DBUS[0]), .pin4(DBUS[1]), .pin5(FreqLatch_pin5),
    .pin6(FreqLatch_pin6), .pin7(DBUS[2]), .pin8(DBUS[3]), .pin9(FreqLatch_pin9), .pin19(FreqLatch_pin19),
    .pin18(DBUS[7]), .pin17(DBUS[6]), .pin16(FreqLatch_pin16), .pin15(FreqLatch_pin15), .pin14(DBUS[5]),
    .pin13(DBUS[4]), .pin12(FreqLatch_pin12), .pin11(nPHI2));
  _74161 #(.ShowInternalStructure("true")) CounterHi (
    .pin1(CounterHi_pin1), .pin2(HSync), .pin3(FreqLatch_pin12), .pin4(FreqLatch_pin15),
    .pin5(FreqLatch_pin16), .pin6(FreqLatch_pin19), .pin7(CounterHi_pin7), .pin15(CounterHi_pin15),
    .pin10(CounterHi_pin7), .pin9(CounterHi_pin9));  // open: pin14, pin13, pin12, pin11
  _74161 #(.ShowInternalStructure("true")) CounterLo (
    .pin1(CounterLo_pin1), .pin2(HSync), .pin3(FreqLatch_pin2), .pin4(FreqLatch_pin5), .pin5(FreqLatch_pin6),
    .pin6(FreqLatch_pin9), .pin7(CounterLo_pin7), .pin15(CounterHi_pin7), .pin10(CounterLo_pin7),
    .pin9(CounterHi_pin9));  // open: pin14, pin13, pin12, pin11
  not not_1 (CounterHi_pin9, CounterHi_pin15);
  T_Flip_Flop t_ff_1 (.clk(HSync), .T(CounterHi_pin15), .Q(SND));  // open: Qn, preset, reset
  LED led_1 (.in(SND));
  // also tied to VCC on the sheet: {CounterHi_pin1, CounterLo_pin1, CounterLo_pin7}

  // Notes on the sheet:
  //   nWR: initial=0x1
  //   DBUS: initial=0x80
  //   Note: if using 374, NOR nWR with nPHI2
  //   IO address decode
  //   Rising Edge as PHI2 falls
  //   74LS374 ?
  //   15720 Hz
  //   DIV 2
endmodule
