// Logisim project HCountVDP.circ as structural Verilog: 2 circuits, main circuit main
module main (
);

  wire and_1_out, and_2_out, and_3_out, and_4_out, and_5_out, and_6_out, and_7_out, and_8_out, and_9_out,
       and_10_out, and_11_out, and_12_out, and_13_out, and_14_out, and_15_out, and_16_out, and_18_out,
       and_19_out, clock_1_out, d_ff_1_q, d_ff_2_q, d_ff_3_q, d_ff_4_q, j_k_ff_4_q, j_k_ff_5_q, j_k_ff_5_qn,
       j_k_ff_6_q, n74138_1_pin11, n74138_1_pin12, n74138_1_pin15, n74157_1_pin1, n74157_1_pin4,
       n74157_1_pin7, n74157_1_pin9, n74157_1_pin12, n74157_1_pin15, n74157_2_pin15, n74161_1_pin1,
       n74161_1_pin3, n74161_1_pin11, n74161_1_pin14, n74161_2_pin1, n74161_2_pin3, n74161_2_pin4,
       n74161_2_pin5, n74161_2_pin6, n74161_2_pin7, n74161_2_pin9, n74161_3_pin1, n74161_3_pin3,
       n74161_3_pin4, n74161_3_pin5, n74161_3_pin6, n74161_3_pin7, n74161_4_pin1, n74161_4_pin2,
       n74161_4_pin3, n74161_4_pin4, n74161_4_pin5, n74161_4_pin6, n74161_4_pin7, n74161_4_pin9,
       n74161_4_pin15, n74161_5_pin1, n74161_5_pin3, n74161_5_pin4, n74161_5_pin5, n74161_5_pin6,
       n74161_5_pin7, n74166_1_pin1, n74166_1_pin2, n74166_1_pin3, n74166_1_pin4, n74166_1_pin5,
       n74166_1_pin6, n74166_1_pin7, n74166_1_pin9, n74166_1_pin10, n74166_1_pin11, n74166_1_pin12,
       n74166_1_pin13, n74166_1_pin14, n74273_1_pin1, n74273_1_pin2, n74273_1_pin5, n74273_1_pin6,
       n74273_1_pin9, n74273_1_pin11, n74273_1_pin12, n74273_1_pin15, n74273_1_pin16, n74273_1_pin19,
       n74273_2_pin1, not_4_out, not_5_out, not_6_out, not_7_out, not_8_out, not_9_out, not_10_out,
       not_11_out, not_13_out, not_14_out, not_15_out, not_16_out, not_17_out, not_18_out, not_20_out,
       not_21_out, not_22_out, or_1_out, or_2_out, or_7_out, or_8_out, undriven;
  wire [3:0] n74153_2_pin5, n74153_2_pin7, n74157_2_pin4, or_6_out, register_2_q;
  wire [7:0] multiplexer_1_out, multiplexer_3_out, n74273_1_pin3, n74273_2_pin3, register_1_q,
       rgb_video_1_p6, undriven_2;
  wire [8:0] n74161_1_pin13, n74161_5_pin14;

  // NOT_Gate not_1 is placed but not wired
  J_K_Flip_Flop j_k_ff_1 ();  // open: J, clk, K, Q, Qn, preset, reset
  Clock clock_1 (.out(clock_1_out));
  _74161 #(.ShowInternalStructure("true")) u_74161_1 (
    .pin1(n74161_1_pin1), .pin2(clock_1_out), .pin3(n74161_1_pin3), .pin4(n74161_1_pin3),
    .pin5(n74161_1_pin3), .pin6(n74161_1_pin3), .pin7(n74161_1_pin3), .pin14(n74161_1_pin14),
    .pin13(n74161_1_pin13[0]), .pin12(n74161_1_pin13[1]), .pin11(n74161_1_pin11), .pin10(n74161_1_pin3),
    .pin9(n74161_1_pin3));  // open: pin15
  _74161 #(.ShowInternalStructure("true")) u_74161_2 (
    .pin1(n74161_2_pin1), .pin2(n74161_1_pin11), .pin3(n74161_2_pin3), .pin4(n74161_2_pin4),
    .pin5(n74161_2_pin5), .pin6(n74161_2_pin6), .pin7(n74161_2_pin7), .pin14(n74161_1_pin13[7]),
    .pin13(n74161_1_pin13[8]), .pin10(n74161_2_pin7), .pin9(n74161_2_pin9));  // open: pin15, pin12, pin11
  _74161 #(.ShowInternalStructure("true")) u_74161_3 (
    .pin1(n74161_3_pin1), .pin2(n74161_1_pin11), .pin3(n74161_3_pin3), .pin4(n74161_3_pin4),
    .pin5(n74161_3_pin5), .pin6(n74161_3_pin6), .pin7(n74161_3_pin7), .pin15(n74161_2_pin7),
    .pin14(n74161_1_pin13[3]), .pin13(n74161_1_pin13[4]), .pin12(n74161_1_pin13[5]),
    .pin11(n74161_1_pin13[6]), .pin10(n74161_3_pin7), .pin9(n74161_2_pin9));
  _74161 #(.ShowInternalStructure("true")) u_74161_4 (
    .pin1(n74161_4_pin1), .pin2(n74161_4_pin2), .pin3(n74161_4_pin3), .pin4(n74161_4_pin4),
    .pin5(n74161_4_pin5), .pin6(n74161_4_pin6), .pin7(n74161_4_pin7), .pin15(n74161_4_pin15),
    .pin14(n74161_5_pin14[4]), .pin13(n74161_5_pin14[5]), .pin12(n74161_5_pin14[6]),
    .pin11(n74161_5_pin14[7]), .pin10(n74161_4_pin7), .pin9(n74161_4_pin9));
  _74161 #(.ShowInternalStructure("true")) u_74161_5 (
    .pin1(n74161_5_pin1), .pin2(n74161_4_pin2), .pin3(n74161_5_pin3), .pin4(n74161_5_pin4),
    .pin5(n74161_5_pin5), .pin6(n74161_5_pin6), .pin7(n74161_5_pin7), .pin15(n74161_4_pin7),
    .pin14(n74161_5_pin14[0]), .pin13(n74161_5_pin14[1]), .pin12(n74161_5_pin14[2]),
    .pin11(n74161_5_pin14[3]), .pin10(n74161_5_pin7), .pin9(n74161_4_pin9));
  J_K_Flip_Flop j_k_ff_2 (
    .J(n74161_4_pin15), .clk(n74161_4_pin2), .K(and_3_out), .Q(n74161_5_pin14[8]));  // open: Qn, preset, reset
  and and_1 (and_1_out, n74161_1_pin11, n74161_1_pin13[1], n74161_1_pin13[0], n74161_1_pin14);
  and and_2 (and_2_out, n74161_1_pin13[7], n74161_1_pin13[8], n74161_1_pin13[6]);
  not not_2 (n74161_2_pin9, and_2_out);
  and and_3 (and_3_out, n74161_5_pin14[8], and_4_out);
  not not_3 (n74161_4_pin9, and_3_out);
  not not_4 (not_4_out, n74161_1_pin13[7]);
  not not_5 (not_5_out, n74161_5_pin14[7]);
  and and_4 (and_4_out, n74161_5_pin14[2], n74161_5_pin14[0]);
  and and_5 (and_5_out, n74161_1_pin13[8], not_4_out, n74161_1_pin13[6]);
  D_Flip_Flop d_ff_1 (.clk(n74161_4_pin2), .D(and_3_out), .Q(d_ff_1_q));  // open: Qn, preset, reset
  and and_6 (and_6_out, n74161_1_pin13[3], n74161_1_pin13[7], n74161_1_pin13[8]);
  _74138 #(.ShowInternalStructure("true")) u_74138_1 (
    .pin1(n74161_5_pin14[3]), .pin2(n74161_5_pin14[4]), .pin3(n74161_5_pin14[5]), .pin4(n74161_5_pin14[8]),
    .pin5(not_5_out), .pin6(n74161_5_pin14[6]), .pin15(n74138_1_pin15), .pin12(n74138_1_pin12),
    .pin11(n74138_1_pin11));  // open: pin7, pin14, pin13, pin10, pin9
  not not_6 (not_6_out, and_7_out);
  and and_7 (and_7_out, and_5_out, n74161_1_pin13[5], n74161_1_pin13[4]);
  and and_8 (and_8_out, and_5_out, j_k_ff_5_qn, n74161_2_pin7);
  not not_7 (not_7_out, n74138_1_pin12);
  not not_8 (not_8_out, n74138_1_pin11);
  not not_9 (not_9_out, n74138_1_pin15);
  and and_9 (and_9_out, and_5_out, not_6_out, n74161_1_pin13[4]);
  not not_10 (not_10_out, n74161_1_pin13[8]);
  // Probe on not_10_out
  and and_10 (and_10_out, not_7_out, and_4_out);
  not not_11 (not_11_out, n74161_1_pin11);
  J_K_Flip_Flop #(.trigger("falling")) j_k_ff_3 (
    .J(and_9_out), .clk(not_11_out), .K(and_7_out), .Q(n74161_4_pin2));  // open: Qn, preset, reset
  D_Flip_Flop d_ff_2 (.clk(n74161_1_pin11), .D(not_10_out), .Q(d_ff_2_q));  // open: Qn, preset, reset
  J_K_Flip_Flop #(.trigger("falling")) j_k_ff_4 (
    .J(and_8_out), .clk(not_11_out), .K(and_6_out), .Q(j_k_ff_4_q));  // open: Qn, preset, reset
  J_K_Flip_Flop #(.trigger("falling")) j_k_ff_5 (
    .J(and_10_out), .clk(not_11_out), .K(not_8_out), .Q(j_k_ff_5_q), .Qn(j_k_ff_5_qn));  // open: preset, reset
  J_K_Flip_Flop #(.trigger("falling")) j_k_ff_6 (
    .J(d_ff_1_q), .clk(not_11_out), .K(not_9_out), .Q(j_k_ff_6_q));  // open: Qn, preset, reset
  not not_12 (n74161_1_pin13[2], n74161_1_pin11);
  and and_11 (and_11_out, d_ff_2_q, j_k_ff_6_q);
  // Probe on n74161_1_pin13
  or or_1 (or_1_out, and_12_out, and_13_out);
  // RGB_Video #(.cursor("No Cursor"), .height(262), .scale(1), .width(458)) rgb_video_1: pin names not known; wires that end beside it: 1'b0, n74161_1_pin14, 1'b1, n74161_1_pin13, n74161_5_pin14, rgb_video_1_p6
  // Probe on n74161_5_pin14
  and and_12 (and_12_out, n74161_1_pin13[0], 1'b0);
  and and_13 (and_13_out, n74161_1_pin14, not_13_out);
  Multiplexer #(.width(8)) multiplexer_1 (.in0(register_1_q), .in1(8'hb), .out(multiplexer_1_out), .sel(j_k_ff_4_q));
  not not_13 (not_13_out, 1'b0);
  Multiplexer #(.width(8)) multiplexer_2 (.in0(multiplexer_3_out), .in1(8'hc), .out(rgb_video_1_p6), .sel(j_k_ff_5_q));
  Multiplexer #(.width(8)) multiplexer_3 (
    .in0(multiplexer_1_out), .in1(8'hd), .out(multiplexer_3_out), .sel(n74161_4_pin2));
  Register register_1 (.D({4'b0000, n74153_2_pin7}), .en(1'b1), .Q(register_1_q), .clk(or_1_out));  // open: clr
  // Probe on j_k_ff_5_q
  or or_2 (or_2_out, not_10_out, and_11_out);
  _74273 #(.ShowInternalStructure("true")) u_74273_1 (
    .pin1(n74273_1_pin1), .pin2(n74273_1_pin2), .pin3(n74273_1_pin3[0]), .pin4(n74273_1_pin3[1]),
    .pin5(n74273_1_pin5), .pin6(n74273_1_pin6), .pin7(n74273_1_pin3[2]), .pin8(n74273_1_pin3[3]),
    .pin9(n74273_1_pin9), .pin19(n74273_1_pin19), .pin18(n74273_1_pin3[7]), .pin17(n74273_1_pin3[6]),
    .pin16(n74273_1_pin16), .pin15(n74273_1_pin15), .pin14(n74273_1_pin3[5]), .pin13(n74273_1_pin3[4]),
    .pin12(n74273_1_pin12), .pin11(n74273_1_pin11));
  not not_14 (not_14_out, and_1_out);
  not not_15 (not_15_out, not_14_out);
  and and_14 (and_14_out, not_15_out, not_18_out);
  not not_16 (not_16_out, and_14_out);
  D_Flip_Flop d_ff_3 (.clk(n74166_1_pin7), .D(n74166_1_pin13), .Q(d_ff_3_q), .reset(not_13_out));  // open: Qn, preset
  not not_17 (not_17_out, and_11_out);
  _74166 #(.ShowInternalStructure("true")) u_74166_1 (
    .pin1(n74166_1_pin1), .pin2(n74166_1_pin2), .pin3(n74166_1_pin3), .pin4(n74166_1_pin4),
    .pin5(n74166_1_pin5), .pin6(n74166_1_pin6), .pin7(n74166_1_pin7), .pin15(not_16_out),
    .pin14(n74166_1_pin14), .pin13(n74166_1_pin13), .pin12(n74166_1_pin12), .pin11(n74166_1_pin11),
    .pin10(n74166_1_pin10), .pin9(n74166_1_pin9));
  _74153 #(.ShowInternalStructure("true")) u_74153_1 (
    .pin1(not_17_out), .pin2(d_ff_3_q), .pin3(n74273_1_pin16), .pin4(n74273_1_pin6), .pin5(n74153_2_pin5[2]),
    .pin6(register_2_q[2]), .pin7(n74153_2_pin7[2]), .pin15(not_17_out), .pin14(n74166_1_pin13),
    .pin13(n74273_1_pin19), .pin12(n74273_1_pin9), .pin11(n74153_2_pin5[3]), .pin10(register_2_q[3]),
    .pin9(n74153_2_pin7[3]));
  _74157 #(.ShowInternalStructure("true")) u_74157_1 (
    .pin1(n74157_1_pin1), .pin2(n74273_1_pin3[0]), .pin3(n74166_1_pin14), .pin4(n74157_1_pin4),
    .pin5(n74273_1_pin3[1]), .pin6(n74166_1_pin12), .pin7(n74157_1_pin7), .pin15(n74157_1_pin15),
    .pin14(n74273_1_pin3[2]), .pin13(n74166_1_pin10), .pin12(n74157_1_pin12), .pin11(n74273_1_pin3[3]),
    .pin10(n74166_1_pin11), .pin9(n74157_1_pin9));
  not not_18 (not_18_out, n74157_1_pin1);
  or or_3 (or_6_out[3], n74157_1_pin12, and_15_out);
  or or_4 (or_6_out[2], n74157_1_pin9, and_15_out);
  not not_19 (n74166_1_pin7, n74161_1_pin14);
  or or_5 (or_6_out[1], n74157_1_pin7, and_15_out);
  or or_6 (or_6_out[0], n74157_1_pin4, and_15_out);
  D_Flip_Flop d_ff_4 (.clk(n74166_1_pin7), .D(not_15_out), .Q(d_ff_4_q));  // open: Qn, preset, reset
  Register #(.width(4)) register_2 (.D(or_6_out), .en(1'b1), .Q(register_2_q), .clk(or_7_out));  // open: clr
  or or_7 (or_7_out, and_19_out, and_15_out, 1'b0);
  _74153 #(.ShowInternalStructure("true")) u_74153_2 (
    .pin1(not_17_out), .pin2(d_ff_3_q), .pin3(n74273_1_pin12), .pin4(n74273_1_pin2), .pin5(n74153_2_pin5[0]),
    .pin6(register_2_q[0]), .pin7(n74153_2_pin7[0]), .pin15(not_17_out), .pin14(n74166_1_pin13),
    .pin13(n74273_1_pin15), .pin12(n74273_1_pin5), .pin11(n74153_2_pin5[1]), .pin10(register_2_q[1]),
    .pin9(n74153_2_pin7[1]));
  _74157 #(.ShowInternalStructure("true")) u_74157_2 (
    .pin1(n74157_1_pin1), .pin2(n74273_1_pin3[4]), .pin3(n74166_1_pin14), .pin4(n74157_2_pin4[0]),
    .pin5(n74273_1_pin3[5]), .pin6(n74166_1_pin12), .pin7(n74157_2_pin4[1]), .pin15(n74157_2_pin15),
    .pin14(n74273_1_pin3[7]), .pin13(n74166_1_pin10), .pin12(n74157_2_pin4[3]), .pin11(n74273_1_pin3[6]),
    .pin10(n74166_1_pin11), .pin9(n74157_2_pin4[2]));
  not not_20 (not_20_out, or_2_out);
  Register #(.width(4)) register_3 (.D(n74157_2_pin4), .en(1'b1), .Q(n74153_2_pin5), .clk(or_8_out), .clr(and_15_out));
  or or_8 (or_8_out, and_18_out, 1'b0);
  and and_15 (and_15_out, not_20_out, 1'b1);
  not not_21 (not_21_out, n74166_1_pin4);
  and and_16 (and_16_out, n74166_1_pin2, n74166_1_pin3, not_21_out);
  and and_17 (n74157_1_pin1, 1'b1, and_16_out);
  and and_18 (and_18_out, n74157_1_pin1, n74166_1_pin5, d_ff_4_q);
  and and_19 (and_19_out, n74157_1_pin1, not_22_out, d_ff_4_q);
  _74273 #(.ShowInternalStructure("true")) u_74273_2 (
    .pin1(n74273_2_pin1), .pin2(n74166_1_pin14), .pin3(n74273_2_pin3[0]), .pin4(n74273_2_pin3[1]),
    .pin5(n74166_1_pin12), .pin6(n74166_1_pin11), .pin7(n74273_2_pin3[2]), .pin8(n74273_2_pin3[3]),
    .pin9(n74166_1_pin10), .pin19(n74166_1_pin2), .pin18(n74273_2_pin3[7]), .pin17(n74273_2_pin3[6]),
    .pin16(n74166_1_pin3), .pin15(n74166_1_pin4), .pin14(n74273_2_pin3[5]), .pin13(n74273_2_pin3[4]),
    .pin12(n74166_1_pin5), .pin11(n74161_1_pin11));
  not not_22 (not_22_out, n74166_1_pin5);
  RAM ram_1 (.addr(undriven_2), .we(1'b0), .oe(1'b1), .clk(undriven), .dout(n74273_1_pin3));  // open: din
  // Random #(.trigger("falling")) random_1: pin names not known; wires that end beside it: 1'b1, n74161_1_pin11
  // NOT_Gate not_23 has open pins: in=n74161_1_pin11, out=open
  // Probe on n74273_1_pin3
  // also tied to GND on the sheet: {n74161_2_pin3, n74161_2_pin4, n74161_2_pin5, n74161_2_pin6, n74161_3_pin3, n74161_3_pin4, n74161_3_pin5, n74161_3_pin6, n74161_4_pin3, n74161_4_pin4, n74161_4_pin5, n74161_4_pin6, n74161_5_pin3, n74161_5_pin4, n74161_5_pin5, n74161_5_pin6, n74273_1_pin11, n74166_1_pin6, n74166_1_pin1, n74157_1_pin15, n74157_2_pin15}
  // also tied to VCC on the sheet: {n74161_1_pin1, n74161_2_pin1, n74161_3_pin1, n74161_3_pin7, n74161_4_pin1, n74161_5_pin1, n74161_5_pin7, n74161_1_pin3, n74273_1_pin1, n74166_1_pin9, n74273_2_pin1}

  // Notes on the sheet:
  //   U30 Dual DFF
  //   U31 Dual JK
  //   U32 Tripe 3-AND
  //   U33 Dual JK
  //   U34 Quad 2-AND
  //   U35 4-bit Counter
  //   U36 4-bit Counter
  //   U37 Tripe 3-AND
  //   U38 Hex Inverter
  //   U39 8-bit Shift Register
  //   U40 4-bit Counter
  //   U41 4-bit Counter
  //   U42 1 of 8 Decoder
  //   U43 Dual JK (1/2)
  //   U44 Hex Inverter (5/6)
  //   U44F
  //   U43B
  //   CLK
  //   14.31818 MHz
  //   2 Chips Clock
  //   Increment on /CLK mid-cycle
  //   Address must be stable by \CLK
  //   13 Chips H & V
  //   6-bit H-Count
  //   [0-56]
  //   U35
  //   U36
  //   9-bit V-Count
  //   U43A
  //   U40
  //   U41
  //   VScan= ~(d8+(d7•d6))
  //   U38A
  //   VBlank = 76~543 + 765~4~3 + 765~4~2
  //   VSync = VBL • ~(d4 + d3 + d2) • (d1 + d0)
  //   N/A
  //   7.15909 MHz
  //   3.579545 MHz
  //   1.7897725 MHz
  //   0.894886 MHz
  //   RHC 56
  //   111xxx
  //   U32A
  //   RVC 261
  //   (100 000 101)
  //   RVC
  //   U34B
  //   U38F
  //   1x1
  //   U34A
  //   Work-around for incorrectly timed RCO output
  //   1 in 16
  //   U38B
  //   U44A
  //   U30B
  //   Line Delay
  //   SHB 40
  //   101xxx
  //   U32B
  //   011
  //   Not VSync
  //   RCB 49
  //   11xxx1
  //   U32C
  //   VSync
  //   Not HBlank
  //   U42
  //   HBlank
  //   RHS 46
  //   10111x
  //   U37B
  //   SCB 47
  //   101111
  //   U37C
  //   000
  //   011
  //   100
  //   Colorburst
  //   Not Burst
  //   VBlank
  //   Not VBlank
  //   Negate Negative Edge (74LS73)
  //   Must be rising-edge for 8px delay
  //   U38C
  //   Fetch
  //   U44B
  //   U44C
  //   U44D
  //   HSync
  //   Not HSync
  //   Scan
  //   NotScan
  //   SHS 42
  //   101x1x
  //   U37A
  //   U38D
  //   U31B
  //   Colorburst
  //   U34C
  //   U44E
  //   U31A
  //   HSync
  //   U30A
  //   Visible
  //   U33A
  //   VSync
  //   U33B
  //   Visible
  //   HBlank
  //   Not HBlank
  //   --
  //   --
  //   VBlank
  //   Not VBlank
  //   7.15909 MHz
  //   N/A
  //   Scanout
  //   U34D
  //   VSync
  //   Not VSync
  //   VSync
  //   Not VSync
  //   HSync
  //   Not HSync
  //   Scan
  //   NotScan
  //   HCount
  //   VCount
  //   HSync
  //   Burst
  //   Scanout
  //   DAC Latch
  //   74LS175
  //   VSync
  //   VSync
  //   VDP_2BPP
  //   Most home computers/consoles
  //   use 0 IRE for both Black and Blanking level
  //   (that would eliminate HBlank and VBlank)
  //   Fetch
  //   Last high PCLK in the CLK cycle
  //   Scanout
  //   COL2/3
  //   U38E
  //   nLoad
  //   74LS74
  //   Delay beyond \PCLK edge
  //   Shifter
  //   MUST load on \PCLK aligned with \CLK
  //   U39
  //   FG
  //   MUX
  //   IOQ_FE
  //   \CLK
  //   \PCLK
  //   Col MUX 2,3
  //   FG
  //   74LS175
  //   MUX
  //   Fetch
  //   Inhibit Load of Cx/Dx in Text mode
  //   BG
  //   ?? Chips Pixel Pipe
  //   LoadQ on \PCLK aligned with \CLK
  //   Col MUX 0,1
  //   Hold FG/BG in Reset until Fetch begins
  //   74LS175
  //   BG
  //   Data Bus
  //   IOQ_FD
  //   VDP_TEXT
  //   Cx/Dx decode
  //   Cx/Dx Text
  //   LoadQ
  //   Latch Address at \CLK
  //   MUST latch at /CLK mid-cycle for VDP
  //   VDP Latch
  //   Data ready by /CLK mid-cycle for VDP
  //   Bus CLK 0.89 MHz
endmodule

// DBUS
module PSG (
  input  HSync,
  input  nPHI2,
  input  nWR,
  input  [7:0] DBUS,
  output SND
);

  wire CounterHi_pin1, CounterHi_pin7, CounterHi_pin9, CounterHi_pin15, CounterLo_pin1, CounterLo_pin7,
       FreqLatch_pin2, FreqLatch_pin5, FreqLatch_pin6, FreqLatch_pin9, FreqLatch_pin12, FreqLatch_pin15,
       FreqLatch_pin16, FreqLatch_pin19;

  _74377 #(.ShowInternalStructure("true")) FreqLatch (
    .pin1(nWR), .pin2(FreqLatch_pin2), .pin3(DBUS[0]), .pin4(DBUS[1]), .pin5(FreqLatch_pin5),
    .pin6(FreqLatch_pin6), .pin7(DBUS[2]), .pin8(DBUS[3]), .pin9(FreqLatch_pin9), .pin19(FreqLatch_pin19),
    .pin18(DBUS[7]), .pin17(DBUS[6]), .pin16(FreqLatch_pin16), .pin15(FreqLatch_pin15), .pin14(DBUS[5]),
    .pin13(DBUS[4]), .pin12(FreqLatch_pin12), .pin11(nPHI2));
  _74161 #(.ShowInternalStructure("true")) CounterHi (
    .pin1(CounterHi_pin1), .pin2(HSync), .pin3(FreqLatch_pin12), .pin4(FreqLatch_pin15),
    .pin5(FreqLatch_pin16), .pin6(FreqLatch_pin19), .pin7(CounterHi_pin7), .pin15(CounterHi_pin15),
    .pin10(CounterHi_pin7), .pin9(CounterHi_pin9));  // open: pin14, pin13, pin12, pin11
  _74161 #(.ShowInternalStructure("true")) CounterLo (
    .pin1(CounterLo_pin1), .pin2(HSync), .pin3(FreqLatch_pin2), .pin4(FreqLatch_pin5), .pin5(FreqLatch_pin6),
    .pin6(FreqLatch_pin9), .pin7(CounterLo_pin7), .pin15(CounterHi_pin7), .pin10(CounterLo_pin7),
    .pin9(CounterHi_pin9));  // open: pin14, pin13, pin12, pin11
  not not_1 (CounterHi_pin9, CounterHi_pin15);
  T_Flip_Flop t_ff_1 (.clk(HSync), .T(CounterHi_pin15), .Q(SND));  // open: Qn, preset, reset
  LED led_1 (.in(SND));
  // also tied to VCC on the sheet: {CounterHi_pin1, CounterLo_pin1, CounterLo_pin7}

  // Notes on the sheet:
  //   nWR: initial=0x1
  //   DBUS: initial=0x80
  //   Note: if using 374, NOR nWR with nPHI2
  //   IO address decode
  //   Rising Edge as PHI2 falls
  //   74LS374 ?
  //   15720 Hz
  //   DIV 2
endmodule
