// Logisim project HCount.circ as structural Verilog: 2 circuits, main circuit main
module main (
);

  wire and_3_out, and_4_out, and_5_out, and_6_out, and_7_out, and_8_out, and_9_out, and_10_out, and_12_out,
       and_13_out, and_14_out, and_15_out, and_16_out, and_17_out, and_18_out, and_19_out, and_20_out,
       and_21_out, and_22_out, clock_1_out, d_ff_1_q, d_ff_2_q, d_ff_3_q, n74161_1_pin1, n74161_1_pin3,
       n74161_1_pin4, n74161_1_pin5, n74161_1_pin6, n74161_1_pin7, n74161_1_pin9, n74161_2_pin1,
       n74161_2_pin3, n74161_2_pin4, n74161_2_pin5, n74161_2_pin6, n74161_2_pin7, n74161_2_pin15,
       n74161_3_pin1, n74161_3_pin3, n74161_3_pin4, n74161_3_pin5, n74161_3_pin6, n74161_3_pin7,
       n74161_3_pin9, n74161_3_pin15, n74161_4_pin1, n74161_4_pin3, n74161_4_pin4, n74161_4_pin5,
       n74161_4_pin6, n74161_4_pin7, nor_1_out, nor_2_out, or_1_out, or_2_out, s_r_ff_2_q, s_r_ff_3_q,
       s_r_ff_4_q, s_r_ff_5_q;
  wire [7:0] multiplexer_1_out, multiplexer_2_out, multiplexer_4_out, multiplexer_5_out, multiplexer_6_out,
       rgb_video_1_p5, rgb_video_1_p7;
  wire [8:0] n74161_4_pin14, t_ff_1_q;

  Clock clock_1 (.out(clock_1_out));
  T_Flip_Flop t_ff_1 (.clk(clock_1_out), .T(1'b1), .Q(t_ff_1_q[0]));  // open: Qn, preset, reset
  _74161 #(.ShowInternalStructure("true")) u_74161_1 (
    .pin1(n74161_1_pin1), .pin2(t_ff_1_q[0]), .pin3(n74161_1_pin3), .pin4(n74161_1_pin4),
    .pin5(n74161_1_pin5), .pin6(n74161_1_pin6), .pin7(n74161_1_pin7), .pin14(t_ff_1_q[5]),
    .pin13(t_ff_1_q[6]), .pin12(t_ff_1_q[7]), .pin11(t_ff_1_q[8]), .pin10(n74161_1_pin7), .pin9(n74161_1_pin9));  // open: pin15
  _74161 #(.ShowInternalStructure("true")) u_74161_2 (
    .pin1(n74161_2_pin1), .pin2(t_ff_1_q[0]), .pin3(n74161_2_pin3), .pin4(n74161_2_pin4),
    .pin5(n74161_2_pin5), .pin6(n74161_2_pin6), .pin7(n74161_2_pin7), .pin15(n74161_2_pin15),
    .pin14(t_ff_1_q[1]), .pin13(t_ff_1_q[2]), .pin12(t_ff_1_q[3]), .pin11(t_ff_1_q[4]),
    .pin10(n74161_2_pin7), .pin9(n74161_2_pin7));
  _74161 #(.ShowInternalStructure("true")) u_74161_3 (
    .pin1(n74161_3_pin1), .pin2(t_ff_1_q[0]), .pin3(n74161_3_pin3), .pin4(n74161_3_pin4),
    .pin5(n74161_3_pin5), .pin6(n74161_3_pin6), .pin7(n74161_3_pin7), .pin15(n74161_3_pin15),
    .pin14(n74161_4_pin14[4]), .pin13(n74161_4_pin14[5]), .pin12(n74161_4_pin14[6]),
    .pin11(n74161_4_pin14[7]), .pin10(n74161_3_pin7), .pin9(n74161_3_pin9));
  _74161 #(.ShowInternalStructure("true")) u_74161_4 (
    .pin1(n74161_4_pin1), .pin2(t_ff_1_q[0]), .pin3(n74161_4_pin3), .pin4(n74161_4_pin4),
    .pin5(n74161_4_pin5), .pin6(n74161_4_pin6), .pin7(n74161_4_pin7), .pin15(n74161_3_pin7),
    .pin14(n74161_4_pin14[0]), .pin13(n74161_4_pin14[1]), .pin12(n74161_4_pin14[2]),
    .pin11(n74161_4_pin14[3]), .pin10(n74161_4_pin7), .pin9(n74161_3_pin9));
  and and_1 (n74161_1_pin7, n74161_1_pin9, n74161_2_pin15);
  S_R_Flip_Flop s_r_ff_1 (
    .S(n74161_3_pin15), .clk(t_ff_1_q[0]), .R(and_3_out), .Q(n74161_4_pin14[8]));  // open: Qn, preset, reset
  and and_2 (n74161_4_pin7, t_ff_1_q[8], t_ff_1_q[7], t_ff_1_q[6], t_ff_1_q[2], t_ff_1_q[1]);
  not not_1 (n74161_1_pin9, n74161_4_pin7);
  and and_3 (and_3_out, n74161_4_pin14[8], n74161_4_pin14[2], n74161_4_pin14[1]);
  not not_2 (n74161_3_pin9, and_3_out);
  and and_4 (and_4_out, t_ff_1_q[5], t_ff_1_q[4]);
  and and_5 (and_5_out, ~t_ff_1_q[8], ~t_ff_1_q[7]);  // AND_Gate
  and and_6 (and_6_out, t_ff_1_q[3], t_ff_1_q[2]);
  and and_7 (and_7_out, ~n74161_4_pin14[2], ~n74161_4_pin14[4], n74161_4_pin14[5], and_10_out);  // AND_Gate
  and and_8 (and_8_out, ~n74161_4_pin14[3], ~n74161_4_pin14[4], n74161_4_pin14[5], and_10_out);  // AND_Gate
  and and_9 (and_9_out, n74161_4_pin14[3], n74161_4_pin14[4], ~n74161_4_pin14[5], and_10_out);  // AND_Gate
  and and_10 (and_10_out, n74161_4_pin14[7], n74161_4_pin14[6]);
  // AND_Gate and_11 has open pins: in0=t_ff_1_q[6], in1=and_4_out, in2=t_ff_1_q[3], out=open
  and and_12 (and_12_out, and_5_out, ~t_ff_1_q[6]);  // AND_Gate
  or or_1 (or_1_out, and_7_out, and_8_out, and_9_out);
  nor nor_1 (nor_1_out, n74161_4_pin14[8], and_10_out);
  and and_13 (and_13_out, and_12_out, ~t_ff_1_q[5]);  // AND_Gate
  // Probe on d_ff_1_q
  D_Flip_Flop d_ff_1 (.clk(t_ff_1_q[0]), .D(or_1_out), .Q(d_ff_1_q));  // open: Qn, preset, reset
  D_Flip_Flop d_ff_2 (.clk(t_ff_1_q[0]), .D(nor_1_out), .Q(d_ff_2_q));  // open: Qn, preset, reset
  or or_2 (or_2_out, n74161_4_pin14[0], n74161_4_pin14[1]);
  nor nor_2 (nor_2_out, n74161_4_pin14[2], n74161_4_pin14[3], n74161_4_pin14[4]);
  and and_14 (and_14_out, t_ff_1_q[6], and_6_out);
  and and_15 (and_15_out, and_6_out, and_13_out);
  and and_16 (and_16_out, and_6_out, t_ff_1_q[5]);
  and and_17 (and_17_out, ~t_ff_1_q[8], t_ff_1_q[7], t_ff_1_q[3]);  // AND_Gate
  and and_18 (and_18_out, t_ff_1_q[8], t_ff_1_q[7], t_ff_1_q[3]);
  and and_19 (and_19_out, and_4_out, and_12_out);
  and and_20 (and_20_out, t_ff_1_q[6], t_ff_1_q[2]);
  D_Flip_Flop d_ff_3 (.clk(t_ff_1_q[0]), .D(and_21_out), .Q(d_ff_3_q));  // open: Qn, preset, reset
  and and_21 (and_21_out, d_ff_1_q, or_2_out, nor_2_out);
  S_R_Flip_Flop s_r_ff_2 (
    .S(n74161_4_pin7), .clk(t_ff_1_q[0]), .R(and_14_out), .Q(s_r_ff_2_q));  // open: Qn, preset, reset
  S_R_Flip_Flop s_r_ff_3 (
    .S(and_15_out), .clk(t_ff_1_q[0]), .R(and_16_out), .Q(s_r_ff_3_q));  // open: Qn, preset, reset
  S_R_Flip_Flop s_r_ff_4 (
    .S(and_17_out), .clk(t_ff_1_q[0]), .R(and_18_out), .Q(s_r_ff_4_q));  // open: Qn, preset, reset
  S_R_Flip_Flop s_r_ff_5 (
    .S(and_19_out), .clk(t_ff_1_q[0]), .R(and_20_out), .Q(s_r_ff_5_q));  // open: Qn, preset, reset
  // Probe on d_ff_3_q
  // Probe on s_r_ff_2_q
  // Probe on t_ff_1_q
  // Probe on n74161_4_pin14
  // RGB_Video #(.height(262), .scale(1), .width(458)) rgb_video_1: pin names not known; wires that end beside it: 1'b0, clock_1_out, 1'b1, t_ff_1_q, rgb_video_1_p5, n74161_4_pin14, rgb_video_1_p7
  Multiplexer #(.width(8)) multiplexer_1 (.in0(multiplexer_2_out), .in1(8'he), .out(multiplexer_1_out), .sel(d_ff_1_q));
  Multiplexer #(.width(8)) multiplexer_2 (.in0(8'h60), .in1(rgb_video_1_p5), .out(multiplexer_2_out), .sel(and_22_out));
  and and_22 (and_22_out, s_r_ff_4_q, d_ff_2_q);
  // Random random_1: pin names not known; wires that end beside it: 1'b1, clock_1_out
  Multiplexer #(.width(8)) multiplexer_3 (.in0(multiplexer_4_out), .in1(8'hc), .out(rgb_video_1_p7), .sel(d_ff_3_q));
  Multiplexer #(.width(8)) multiplexer_4 (
    .in0(multiplexer_1_out), .in1(multiplexer_5_out), .out(multiplexer_4_out), .sel(s_r_ff_2_q));
  Multiplexer #(.width(8)) multiplexer_5 (
    .in0(multiplexer_6_out), .in1(8'hb), .out(multiplexer_5_out), .sel(s_r_ff_5_q));
  Multiplexer #(.width(8)) multiplexer_6 (.in0(8'h2b), .in1(8'hd), .out(multiplexer_6_out), .sel(s_r_ff_3_q));
  // also tied to GND on the sheet: {n74161_1_pin3, n74161_1_pin4, n74161_1_pin5, n74161_1_pin6, n74161_2_pin3, n74161_2_pin4, n74161_2_pin5, n74161_2_pin6, n74161_3_pin3, n74161_3_pin4, n74161_3_pin5, n74161_3_pin6, n74161_4_pin3, n74161_4_pin4, n74161_4_pin5, n74161_4_pin6}
  // also tied to VCC on the sheet: {n74161_1_pin1, n74161_2_pin1, n74161_3_pin1, n74161_4_pin1, n74161_2_pin7}

  // Notes on the sheet:
  //   CLK
  //   7.15909 MHz
  //   CLK/2
  //   8-bit H-Count
  //   [0-227]
  //   9-bit V-Count
  //   VScan= ~(d8+(d7•d6))
  //   3.579545 MHz
  //   RHC
  //   VBlank = 76~543 + 765~4~3 + 765~4~2
  //   VSync = VBL • ~(d4 + d3 + d2) • (d1 + d0)
  //   RHC 227
  //   (11100011)
  //   RVC 262
  //   (1 0000 0110)
  //   RVC
  //   11xxx
  //   1111xx
  //   00xxxxxx
  //   11x
  //   000xxxxx
  //   0000xxxx
  //   VBlank
  //   VScan
  //   11xxx
  //   000xxxxx
  //   d5
  //   d1
  //   ~d7 d6 d2
  //   d7 d6 d2
  //   VSync
  //   HBlank
  //   HSync
  //   HScan
  //   Colorburst
  //   HCount
  //   Scan
  //   VCount
  //   HBlank
  //   VBlank
  //   HSync
  //   Burst
  //   VSync
  //   HBlank
  //   Not HBlank
  //   Not VBlank
  //   VSync
  //   Not VSync
  //   --
  //   --
  //   VBlank
  //   HBlank
  //   Not HBlank
  //   VSync
  //   Not VSync
  //   VSync
  //   Not VSync
  //   HSync
  //   Not HSync
  //   Scan
  //   NotScan
  //   Colorburst
  //   Not Burst
  //   VBlank
  //   Not VBlank
  //   HSync
  //   Not HSync
  //   Scan
  //   NotScan
endmodule

// DBUS
module PSG (
  input  HSync,
  input  nPHI2,
  input  nWR,
  input  [7:0] DBUS,
  output SND
);

  wire CounterHi_pin1, CounterHi_pin7, CounterHi_pin9, CounterHi_pin15, CounterLo_pin1, CounterLo_pin7,
       FreqLatch_pin2, FreqLatch_pin5, FreqLatch_pin6, FreqLatch_pin9, FreqLatch_pin12, FreqLatch_pin15,
       FreqLatch_pin16, FreqLatch_pin19;

  _74377 #(.ShowInternalStructure("true")) FreqLatch (
    .pin1(nWR), .pin2(FreqLatch_pin2), .pin3(DBUS[0]), .pin4(DBUS[1]), .pin5(FreqLatch_pin5),
    .pin6(FreqLatch_pin6), .pin7(DBUS[2]), .pin8(DBUS[3]), .pin9(FreqLatch_pin9), .pin19(FreqLatch_pin19),
    .pin18(DBUS[7]), .pin17(DBUS[6]), .pin16(FreqLatch_pin16), .pin15(FreqLatch_pin15), .pin14(DBUS[5]),
    .pin13(DBUS[4]), .pin12(FreqLatch_pin12), .pin11(nPHI2));
  _74161 #(.ShowInternalStructure("true")) CounterHi (
    .pin1(CounterHi_pin1), .pin2(HSync), .pin3(FreqLatch_pin12), .pin4(FreqLatch_pin15),
    .pin5(FreqLatch_pin16), .pin6(FreqLatch_pin19), .pin7(CounterHi_pin7), .pin15(CounterHi_pin15),
    .pin10(CounterHi_pin7), .pin9(CounterHi_pin9));  // open: pin14, pin13, pin12, pin11
  _74161 #(.ShowInternalStructure("true")) CounterLo (
    .pin1(CounterLo_pin1), .pin2(HSync), .pin3(FreqLatch_pin2), .pin4(FreqLatch_pin5), .pin5(FreqLatch_pin6),
    .pin6(FreqLatch_pin9), .pin7(CounterLo_pin7), .pin15(CounterHi_pin7), .pin10(CounterLo_pin7),
    .pin9(CounterHi_pin9));  // open: pin14, pin13, pin12, pin11
  not not_1 (CounterHi_pin9, CounterHi_pin15);
  T_Flip_Flop t_ff_1 (.clk(HSync), .T(CounterHi_pin15), .Q(SND));  // open: Qn, preset, reset
  LED led_1 (.in(SND));
  // also tied to VCC on the sheet: {CounterHi_pin1, CounterLo_pin1, CounterLo_pin7}

  // Notes on the sheet:
  //   nWR: initial=0x1
  //   DBUS: initial=0x80
  //   Note: if using 374, NOR nWR with nPHI2
  //   IO address decode
  //   Rising Edge as PHI2 falls
  //   74LS374 ?
  //   15720 Hz
  //   DIV 2
endmodule
